// Logisim project v2.circ as structural Verilog: 7 circuits, main circuit ui
module ui (
);

  wire button_1_out, button_2_out, button_3_out, button_4_out, button_5_out, field_1_game_over,
       field_1_pause_out;
  wire [7:0] field_1_next_1, field_1_next_2, field_1_next_3, field_1_next_4, field_1_next_5, field_1_next_6;
  wire [9:0] field_1_row_1, field_1_row_2, field_1_row_3, field_1_row_4, field_1_row_5, field_1_row_6,
       field_1_row_7, field_1_row_8, field_1_row_9, field_1_row_10, field_1_row_11, field_1_row_12,
       field_1_row_13, field_1_row_14, field_1_row_15, field_1_row_16, field_1_row_17, field_1_row_18,
       field_1_row_19, field_1_row_20;
  wire [31:0] field_1_score;

  DotMatrix #(.inputtype("row"), .matrixcols(10), .matrixrows(20)) dotmatrix_1 (
    .row0(field_1_row_1), .row1(field_1_row_2), .row2(field_1_row_3), .row3(field_1_row_4),
    .row4(field_1_row_5), .row5(field_1_row_6), .row6(field_1_row_7), .row7(field_1_row_8),
    .row8(field_1_row_9), .row9(field_1_row_10), .row10(field_1_row_11), .row11(field_1_row_12),
    .row12(field_1_row_13), .row13(field_1_row_14), .row14(field_1_row_15), .row15(field_1_row_16),
    .row16(field_1_row_17), .row17(field_1_row_18), .row18(field_1_row_19), .row19(field_1_row_20));
  field field_1 (
    .row_1(field_1_row_1), .row_2(field_1_row_2), .row_3(field_1_row_3), .row_4(field_1_row_4),
    .row_5(field_1_row_5), .row_6(field_1_row_6), .row_7(field_1_row_7), .row_8(field_1_row_8),
    .row_9(field_1_row_9), .row_10(field_1_row_10), .row_11(field_1_row_11), .row_12(field_1_row_12),
    .row_13(field_1_row_13), .row_14(field_1_row_14), .row_15(field_1_row_15), .row_16(field_1_row_16),
    .row_17(field_1_row_17), .row_18(field_1_row_18), .row_19(field_1_row_19), .row_20(field_1_row_20),
    .move_left(button_1_out), .move_right(button_3_out), .next_1(field_1_next_1), .next_2(field_1_next_2),
    .next_3(field_1_next_3), .next_4(field_1_next_4), .next_5(field_1_next_5), .next_6(field_1_next_6),
    .rotate(button_2_out), .pause(button_4_out), .score(field_1_score), .pause_out(field_1_pause_out),
    .game_over(field_1_game_over), .restart(button_5_out));
  Button button_1 (.out(button_1_out));
  Button button_2 (.out(button_2_out));
  DotMatrix #(.inputtype("row"), .matrixcols(8), .matrixrows(6)) dotmatrix_2 (
    .row0(field_1_next_1), .row1(field_1_next_2), .row2(field_1_next_3), .row3(field_1_next_4),
    .row4(field_1_next_5), .row5(field_1_next_6));
  // Probe on field_1_score
  Button button_3 (.out(button_3_out));
  LED GAME_OVER (.in(field_1_game_over));
  LED ON_PAUSE (.in(field_1_pause_out));
  Button button_4 (.out(button_4_out));
  Button button_5 (.out(button_5_out));

  // Notes on the sheet:
  //   TETRIS!
  //   ROTATE
  //   LEFT
  //   RIGHT
  //   NEXT
  //   SCORE
  //   PAUSE
  //   RESTART
endmodule

module proc (
  input  pause,
  input  restart,
  input  game_over,
  output out_4
);

  wire and_3_out, cdm_8_mark5_1_p4, cdm_8_mark5_1_p5, cdm_8_mark5_1_p7, cdm_8_mark5_1_p8, cdm_8_mark5_1_p9,
       cdm_8_mark5_1_p10, cdm_8_mark5_1_p11, cdm_8_mark5_1_p12, cdm_8_mark5_1_p13, clock_1_out,
       decoder_1_out0, decoder_1_out1, IAck, IOsel, IRQ, not_1_out, not_2_out, READwrite;
  wire [2:0] vec;
  wire [3:0] IOaddr;
  wire [7:0] cdm_8_mark5_1_p16, cdm_8_mark5_1_p17, IOdat;
  wire [7:4] cdm_8_mark5_1_p15;

  Clock clock_1 (.out(clock_1_out));
  and and_1 (out_4, ~pause, ~game_over, clock_1_out);  // AND_Gate
  // Probe on cdm_8_mark5_1_p7
  // Probe on cdm_8_mark5_1_p5
  // Probe on cdm_8_mark5_1_p4
  // Probe on cdm_8_mark5_1_p8
  // Probe on cdm_8_mark5_1_p10
  // Probe on cdm_8_mark5_1_p9
  // Probe on cdm_8_mark5_1_p11
  and and_2 (IOsel, cdm_8_mark5_1_p15[4], cdm_8_mark5_1_p15[5], cdm_8_mark5_1_p15[6], cdm_8_mark5_1_p15[7], decoder_1_out1);
  Decoder #(.disabled(0)) decoder_1 (
    .out0(decoder_1_out0), .out1(decoder_1_out1), .sel(cdm_8_mark5_1_p12), .en(cdm_8_mark5_1_p13));
  // CdM_8_mark5 cdm_8_mark5_1: pin names not known; wires that end beside it: IRQ, vec, IAck, cdm_8_mark5_1_p4, cdm_8_mark5_1_p5, out_4, cdm_8_mark5_1_p7, cdm_8_mark5_1_p8, cdm_8_mark5_1_p9, cdm_8_mark5_1_p10, cdm_8_mark5_1_p11, cdm_8_mark5_1_p12, cdm_8_mark5_1_p13, READwrite, {cdm_8_mark5_1_p15, IOaddr}, cdm_8_mark5_1_p16, cdm_8_mark5_1_p17
  not not_1 (not_1_out, READwrite);
  assign IOdat = not_1_out ? cdm_8_mark5_1_p16 : 8'bz;  // Controlled_Buffer controlled_buffer_1
  assign cdm_8_mark5_1_p17 = READwrite ? IOdat : 8'bz;  // Controlled_Buffer controlled_buffer_2
  and and_3 (and_3_out, decoder_1_out1, ~IOsel);  // AND_Gate
  // Probe on {cdm_8_mark5_1_p15, IOaddr}
  not not_2 (not_2_out, out_4);
  // Probe on IOdat
  RAM ram_1 (
    .addr({cdm_8_mark5_1_p15, IOaddr}), .data(IOdat), .sel(and_3_out), .clk(not_2_out), .ld(READwrite));  // open: clr
  ROM rom_1 (.addr({cdm_8_mark5_1_p15, IOaddr}), .data(IOdat), .sel(decoder_1_out0));

  // Other names for the same wires on the sheet: clk = out_4

  // Notes on the sheet:
  //   contents of rom_1 (hex, n*v repeats v):
  //   cd f0 d0 0 d1 10 a4 d1 11 a4 d0 f0 d1 1 a1 c0 d0 17 c0 d0 80 c0 d9 c4 3f d0 b2 d6 a0 d0 10 b0 d1 11
  //   b5 71 e1 29 d5 ee 1d b2 8c d1 f 44 d1 10 a4 a e0 40 d 25 25 25 2f 17 d1 30 39 17 ee 58 d0 b9 d6 a0 e
  //   4*9f d1 f 4d d6 6a d1 f 49 d6 6a d0 b2 d6 a0 3f ee 1d 30 31 32 33 34 35 36 37 38 39 61 62 63 64 65
  //   66 d0 5a 14 f0 d1 f1 a4 d7 ce d0 f1 b2 d1 11 b5 8d d0 f 41 d0 10 b0 74 e0 9a 89 d0 f 41 d0 f1 a2 d0
  //   a 78 e1 90 3a a6 8d d0 f 41 d0 11 a1 ee 9e d0 ab d6 a0 cf d9 d1 f1 f2 8c a e0 aa a6 ee a2 d7 77 61
  //   69 74 21 d 0 d 64 65 63 3a 20 0 68 65 78 3a 20 54*0 72
endmodule

module field (
  input  move_left,
  input  pause,
  input  move_right,
  input  restart,
  input  rotate,
  output [7:0] next_1,
  output [9:0] row_1,
  output [7:0] next_2,
  output [9:0] row_2,
  output [7:0] next_3,
  output [9:0] row_3,
  output [7:0] next_4,
  output [7:0] next_5,
  output [9:0] row_4,
  output [7:0] next_6,
  output [9:0] row_5,
  output [9:0] row_6,
  output [31:0] score,
  output [9:0] row_7,
  output pause_out,
  output [9:0] row_8,
  output game_over,
  output [9:0] row_9,
  output [9:0] row_10,
  output [9:0] row_11,
  output [9:0] row_12,
  output [9:0] row_13,
  output [9:0] row_14,
  output [9:0] row_15,
  output [9:0] row_16,
  output [9:0] row_17,
  output [9:0] row_18,
  output [9:0] row_19,
  output [9:0] row_20
);

  wire and_1_out, and_2_out, and_3_out, and_4_out, and_5_out, bottom, clk, collision_1_collision_down,
       collision_1_collision_left, collision_1_collision_right, collision_down, collision_left,
       collision_right, comparator_1_eq, comparator_2_eq, comparator_3_eq, delete, deletion, game_clk,
       get_next, left_bord, no_placement, not_2_out, not_3_out, not_4_out, not_5_out, not_6_out, not_7_out,
       not_8_out, not_9_out, not_10_out, not_11_out, not_12_out, not_13_out, not_14_out, not_15_out,
       not_16_out, not_17_out, not_18_out, not_19_out, not_20_out, not_21_out, not_22_out, not_23_out,
       or_5_out, or_6_out, or_7_out, or_8_out, or_10_out, right_bord, save, score_en, side_move, spawn,
       spawn_new;
  wire [1:0] counter;
  wire [3:0] adder_1_out, l_x, multiplexer_1_out, multiplexer_2_out, r_x, subtractor_1_out, x;
  wire [7:0] collision_1_next_line, collision_2_next_line, collision_3_next_line, collision_4_next_line,
       collision_5_next_line, collision_6_next_line, collision_7_next_line, collision_8_next_line,
       collision_9_next_line, collision_10_next_line, collision_11_next_line, collision_12_next_line,
       collision_13_next_line, collision_14_next_line, collision_15_next_line, collision_16_next_line,
       collision_17_next_line, collision_18_next_line, collision_19_next_line, full_counter,
       sprite_mover_1_full_count_out, sprite_mover_1_next_line, sprite_mover_2_full_count_out,
       sprite_mover_2_next_line, sprite_mover_3_full_count_out, sprite_mover_3_next_line,
       sprite_mover_4_full_count_out, sprite_mover_4_next_line, sprite_mover_5_full_count_out,
       sprite_mover_5_next_line, sprite_mover_6_full_count_out, sprite_mover_6_next_line,
       sprite_mover_7_full_count_out, sprite_mover_7_next_line, sprite_mover_8_full_count_out,
       sprite_mover_8_next_line, sprite_mover_9_full_count_out, sprite_mover_9_next_line,
       sprite_mover_10_full_count_out, sprite_mover_10_next_line, sprite_mover_11_full_count_out,
       sprite_mover_11_next_line, sprite_mover_12_full_count_out, sprite_mover_12_next_line,
       sprite_mover_13_full_count_out, sprite_mover_13_next_line, sprite_mover_14_full_count_out,
       sprite_mover_14_next_line, sprite_mover_15_full_count_out, sprite_mover_15_next_line,
       sprite_mover_16_full_count_out, sprite_mover_16_next_line, sprite_mover_17_full_count_out,
       sprite_mover_17_next_line, sprite_mover_18_full_count_out, sprite_mover_18_next_line,
       sprite_mover_19_full_count_out, sprite_mover_19_next_line, sprite_mover_20_full_count_out,
       sprite_mover_20_next_line, sprite_mover_21_full_count_out, sprite_mover_21_next_line,
       sprite_mover_22_full_count_out, sprite_mover_22_next_line, sprite_mover_23_full_count_out,
       sprite_mover_23_next_line, sprite_mover_24_full_count_out, sprite_mover_24_next_line,
       sprite_mover_25_full_count_out, sprite_mover_25_next_line, sprite_mover_26_full_count_out,
       sprite_mover_26_next_line, subtractor_2_out, y;
  wire [9:0] f1, f2, f3, f4, l1_b, l20_b, l_1, l_2, l_3, l_4, or_9_out, sprite_mover_1_out,
       sprite_mover_2_out, sprite_mover_3_out, sprite_mover_4_out, sprite_mover_5_out,
       sprite_mover_6_background_out, sprite_mover_6_out, sprite_mover_7_background_out, sprite_mover_7_out,
       sprite_mover_8_background_out, sprite_mover_8_out, sprite_mover_9_background_out, sprite_mover_9_out,
       sprite_mover_10_background_out, sprite_mover_10_out, sprite_mover_11_background_out,
       sprite_mover_11_out, sprite_mover_12_background_out, sprite_mover_12_out,
       sprite_mover_13_background_out, sprite_mover_13_out, sprite_mover_14_background_out,
       sprite_mover_14_out, sprite_mover_15_background_out, sprite_mover_15_out,
       sprite_mover_16_background_out, sprite_mover_16_out, sprite_mover_17_background_out,
       sprite_mover_17_out, sprite_mover_18_background_out, sprite_mover_18_out,
       sprite_mover_19_background_out, sprite_mover_19_out, sprite_mover_20_background_out,
       sprite_mover_20_out, sprite_mover_21_background_out, sprite_mover_21_out,
       sprite_mover_22_background_out, sprite_mover_22_out, sprite_mover_23_background_out,
       sprite_mover_23_out, sprite_mover_24_out, sprite_mover_25_out, sprite_mover_26_out, xor_1_out;
  wire [15:0] bit_extender_1_out, bit_extender_2_out, bit_extender_3_out, bit_extender_4_out, curr_figure,
       next_figure, shifter_1_out, shifter_2_out, shifter_3_out, shifter_4_out, shifter_5_out, shifter_6_out,
       shifter_7_out, shifter_8_out;
  wire [31:0] multiplexer_3_out, multiplexer_4_out, score_temp;

  DotMatrix #(.inputtype("row"), .matrixcols(10), .matrixrows(23)) dotmatrix_1 (
    .row0(l_3), .row1(l_2), .row2(l_1), .row3(row_1), .row4(row_2), .row5(row_3), .row6(row_4), .row7(row_5),
    .row8(row_6), .row9(row_7), .row10(row_8), .row11(row_9), .row12(row_10), .row13(row_11), .row14(row_12),
    .row15(row_13), .row16(row_14), .row17(row_15), .row18(row_16), .row19(row_17), .row20(row_18),
    .row21(row_19), .row22(row_20));
  or or_1 (collision_left, left_bord, collision_1_collision_left);
  or or_2 (collision_down, bottom, collision_1_collision_down);
  or or_3 (collision_right, right_bord, collision_1_collision_right);
  collision collision_1 (
    .y_placement(y), .sprite_top(f1), .sprite_topmid(f2), .sprite_botmid(f3), .sprite_bottom(f4),
    .background_row(l1_b), .next_line(collision_1_next_line), .collision_left(collision_1_collision_left),
    .collision_right(collision_1_collision_right), .collision_down(collision_1_collision_down));  // open: line_in
  collision collision_2 (
    .line_in(collision_1_next_line), .y_placement(y), .sprite_top(f1), .sprite_topmid(f2),
    .sprite_botmid(f3), .sprite_bottom(f4), .background_row(sprite_mover_6_background_out),
    .next_line(collision_2_next_line), .collision_left(collision_1_collision_left),
    .collision_right(collision_1_collision_right), .collision_down(collision_1_collision_down));
  collision collision_3 (
    .line_in(collision_2_next_line), .y_placement(y), .sprite_top(f1), .sprite_topmid(f2),
    .sprite_botmid(f3), .sprite_bottom(f4), .background_row(sprite_mover_7_background_out),
    .next_line(collision_3_next_line), .collision_left(collision_1_collision_left),
    .collision_right(collision_1_collision_right), .collision_down(collision_1_collision_down));
  collision collision_4 (
    .line_in(collision_3_next_line), .y_placement(y), .sprite_top(f1), .sprite_topmid(f2),
    .sprite_botmid(f3), .sprite_bottom(f4), .background_row(sprite_mover_8_background_out),
    .next_line(collision_4_next_line), .collision_left(collision_1_collision_left),
    .collision_right(collision_1_collision_right), .collision_down(collision_1_collision_down));
  collision collision_5 (
    .line_in(collision_4_next_line), .y_placement(y), .sprite_top(f1), .sprite_topmid(f2),
    .sprite_botmid(f3), .sprite_bottom(f4), .background_row(sprite_mover_9_background_out),
    .next_line(collision_5_next_line), .collision_left(collision_1_collision_left),
    .collision_right(collision_1_collision_right), .collision_down(collision_1_collision_down));
  collision collision_6 (
    .line_in(collision_5_next_line), .y_placement(y), .sprite_top(f1), .sprite_topmid(f2),
    .sprite_botmid(f3), .sprite_bottom(f4), .background_row(sprite_mover_10_background_out),
    .next_line(collision_6_next_line), .collision_left(collision_1_collision_left),
    .collision_right(collision_1_collision_right), .collision_down(collision_1_collision_down));
  collision collision_7 (
    .line_in(collision_6_next_line), .y_placement(y), .sprite_top(f1), .sprite_topmid(f2),
    .sprite_botmid(f3), .sprite_bottom(f4), .background_row(sprite_mover_11_background_out),
    .next_line(collision_7_next_line), .collision_left(collision_1_collision_left),
    .collision_right(collision_1_collision_right), .collision_down(collision_1_collision_down));
  collision collision_8 (
    .line_in(collision_7_next_line), .y_placement(y), .sprite_top(f1), .sprite_topmid(f2),
    .sprite_botmid(f3), .sprite_bottom(f4), .background_row(sprite_mover_12_background_out),
    .next_line(collision_8_next_line), .collision_left(collision_1_collision_left),
    .collision_right(collision_1_collision_right), .collision_down(collision_1_collision_down));
  collision collision_9 (
    .line_in(collision_8_next_line), .y_placement(y), .sprite_top(f1), .sprite_topmid(f2),
    .sprite_botmid(f3), .sprite_bottom(f4), .background_row(sprite_mover_13_background_out),
    .next_line(collision_9_next_line), .collision_left(collision_1_collision_left),
    .collision_right(collision_1_collision_right), .collision_down(collision_1_collision_down));
  collision collision_10 (
    .line_in(collision_9_next_line), .y_placement(y), .sprite_top(f1), .sprite_topmid(f2),
    .sprite_botmid(f3), .sprite_bottom(f4), .background_row(sprite_mover_14_background_out),
    .next_line(collision_10_next_line), .collision_left(collision_1_collision_left),
    .collision_right(collision_1_collision_right), .collision_down(collision_1_collision_down));
  collision collision_11 (
    .line_in(collision_10_next_line), .y_placement(y), .sprite_top(f1), .sprite_topmid(f2),
    .sprite_botmid(f3), .sprite_bottom(f4), .background_row(sprite_mover_15_background_out),
    .next_line(collision_11_next_line), .collision_left(collision_1_collision_left),
    .collision_right(collision_1_collision_right), .collision_down(collision_1_collision_down));
  collision collision_12 (
    .line_in(collision_11_next_line), .y_placement(y), .sprite_top(f1), .sprite_topmid(f2),
    .sprite_botmid(f3), .sprite_bottom(f4), .background_row(sprite_mover_16_background_out),
    .next_line(collision_12_next_line), .collision_left(collision_1_collision_left),
    .collision_right(collision_1_collision_right), .collision_down(collision_1_collision_down));
  collision collision_13 (
    .line_in(collision_12_next_line), .y_placement(y), .sprite_top(f1), .sprite_topmid(f2),
    .sprite_botmid(f3), .sprite_bottom(f4), .background_row(sprite_mover_17_background_out),
    .next_line(collision_13_next_line), .collision_left(collision_1_collision_left),
    .collision_right(collision_1_collision_right), .collision_down(collision_1_collision_down));
  collision collision_14 (
    .line_in(collision_13_next_line), .y_placement(y), .sprite_top(f1), .sprite_topmid(f2),
    .sprite_botmid(f3), .sprite_bottom(f4), .background_row(sprite_mover_18_background_out),
    .next_line(collision_14_next_line), .collision_left(collision_1_collision_left),
    .collision_right(collision_1_collision_right), .collision_down(collision_1_collision_down));
  collision collision_15 (
    .line_in(collision_14_next_line), .y_placement(y), .sprite_top(f1), .sprite_topmid(f2),
    .sprite_botmid(f3), .sprite_bottom(f4), .background_row(sprite_mover_19_background_out),
    .next_line(collision_15_next_line), .collision_left(collision_1_collision_left),
    .collision_right(collision_1_collision_right), .collision_down(collision_1_collision_down));
  collision collision_16 (
    .line_in(collision_15_next_line), .y_placement(y), .sprite_top(f1), .sprite_topmid(f2),
    .sprite_botmid(f3), .sprite_bottom(f4), .background_row(sprite_mover_20_background_out),
    .next_line(collision_16_next_line), .collision_left(collision_1_collision_left),
    .collision_right(collision_1_collision_right), .collision_down(collision_1_collision_down));
  collision collision_17 (
    .line_in(collision_16_next_line), .y_placement(y), .sprite_top(f1), .sprite_topmid(f2),
    .sprite_botmid(f3), .sprite_bottom(f4), .background_row(sprite_mover_21_background_out),
    .next_line(collision_17_next_line), .collision_left(collision_1_collision_left),
    .collision_right(collision_1_collision_right), .collision_down(collision_1_collision_down));
  collision collision_18 (
    .line_in(collision_17_next_line), .y_placement(y), .sprite_top(f1), .sprite_topmid(f2),
    .sprite_botmid(f3), .sprite_bottom(f4), .background_row(sprite_mover_22_background_out),
    .next_line(collision_18_next_line), .collision_left(collision_1_collision_left),
    .collision_right(collision_1_collision_right), .collision_down(collision_1_collision_down));
  collision collision_19 (
    .line_in(collision_18_next_line), .y_placement(y), .sprite_top(f1), .sprite_topmid(f2),
    .sprite_botmid(f3), .sprite_bottom(f4), .background_row(sprite_mover_23_background_out),
    .next_line(collision_19_next_line), .collision_left(collision_1_collision_left),
    .collision_right(collision_1_collision_right), .collision_down(collision_1_collision_down));
  collision collision_20 (
    .line_in(collision_19_next_line), .y_placement(y), .sprite_top(f1), .sprite_topmid(f2),
    .sprite_botmid(f3), .sprite_bottom(f4), .background_row(l20_b),
    .collision_left(collision_1_collision_left), .collision_right(collision_1_collision_right),
    .collision_down(collision_1_collision_down));  // open: next_line
  Pull_Resistor pull_resistor_1 (.node(collision_1_collision_down));
  Pull_Resistor pull_resistor_2 (.node(collision_1_collision_left));
  Pull_Resistor pull_resistor_3 (.node(collision_1_collision_right));
  // Probe on l1_b
  // Probe on sprite_mover_6_background_out
  // Probe on sprite_mover_7_background_out
  // Probe on sprite_mover_8_background_out
  // Probe on sprite_mover_9_background_out
  // Probe on sprite_mover_10_background_out
  // Probe on sprite_mover_11_background_out
  // Probe on sprite_mover_12_background_out
  // Probe on sprite_mover_13_background_out
  // Probe on sprite_mover_14_background_out
  // Probe on sprite_mover_15_background_out
  // Probe on sprite_mover_16_background_out
  // Probe on sprite_mover_17_background_out
  // Probe on sprite_mover_18_background_out
  // Probe on sprite_mover_19_background_out
  // Probe on sprite_mover_20_background_out
  // Probe on sprite_mover_21_background_out
  // Probe on sprite_mover_22_background_out
  // Probe on sprite_mover_23_background_out
  // Probe on l20_b
  sprite_mover sprite_mover_1 (
    .next_line(sprite_mover_1_next_line), .sprite_top(f1), .sprite_topmid(f2), .sprite_botmid(f3),
    .sprite_bottom(f4), .y_placement(y), .out(sprite_mover_1_out), .save_to_background(save),
    .delete_row(delete), .row_out(l_4), .full_count_out(sprite_mover_1_full_count_out), .erase(get_next));  // open: line_in, background_out, full_row_in, full_count_in
  sprite_mover sprite_mover_2 (
    .line_in(sprite_mover_1_next_line), .next_line(sprite_mover_2_next_line), .sprite_top(f1),
    .sprite_topmid(f2), .sprite_botmid(f3), .sprite_bottom(f4), .y_placement(y), .out(sprite_mover_2_out),
    .save_to_background(save), .delete_row(delete), .full_row_in(sprite_mover_1_out), .row_out(l_3),
    .full_count_in(sprite_mover_1_full_count_out), .full_count_out(sprite_mover_2_full_count_out),
    .erase(get_next));  // open: background_out
  sprite_mover sprite_mover_3 (
    .line_in(sprite_mover_2_next_line), .next_line(sprite_mover_3_next_line), .sprite_top(f1),
    .sprite_topmid(f2), .sprite_botmid(f3), .sprite_bottom(f4), .y_placement(y), .out(sprite_mover_3_out),
    .save_to_background(save), .delete_row(delete), .full_row_in(sprite_mover_2_out), .row_out(l_2),
    .full_count_in(sprite_mover_2_full_count_out), .full_count_out(sprite_mover_3_full_count_out),
    .erase(get_next));  // open: background_out
  sprite_mover sprite_mover_4 (
    .line_in(sprite_mover_3_next_line), .next_line(sprite_mover_4_next_line), .sprite_top(f1),
    .sprite_topmid(f2), .sprite_botmid(f3), .sprite_bottom(f4), .y_placement(y), .out(sprite_mover_4_out),
    .save_to_background(save), .delete_row(delete), .full_row_in(sprite_mover_3_out), .row_out(l_1),
    .full_count_in(sprite_mover_3_full_count_out), .full_count_out(sprite_mover_4_full_count_out),
    .erase(get_next));  // open: background_out
  sprite_mover sprite_mover_5 (
    .line_in(sprite_mover_4_next_line), .next_line(sprite_mover_5_next_line), .sprite_top(f1),
    .sprite_topmid(f2), .sprite_botmid(f3), .sprite_bottom(f4), .y_placement(y), .background_out(l1_b),
    .out(sprite_mover_5_out), .save_to_background(save), .delete_row(delete),
    .full_row_in(sprite_mover_4_out), .row_out(row_1), .full_count_in(sprite_mover_4_full_count_out),
    .full_count_out(sprite_mover_5_full_count_out), .erase(restart));
  sprite_mover sprite_mover_6 (
    .line_in(sprite_mover_5_next_line), .next_line(sprite_mover_6_next_line), .sprite_top(f1),
    .sprite_topmid(f2), .sprite_botmid(f3), .sprite_bottom(f4), .y_placement(y),
    .background_out(sprite_mover_6_background_out), .out(sprite_mover_6_out), .save_to_background(save),
    .delete_row(delete), .full_row_in(sprite_mover_5_out), .row_out(row_2),
    .full_count_in(sprite_mover_5_full_count_out), .full_count_out(sprite_mover_6_full_count_out),
    .erase(restart));
  sprite_mover sprite_mover_7 (
    .line_in(sprite_mover_6_next_line), .next_line(sprite_mover_7_next_line), .sprite_top(f1),
    .sprite_topmid(f2), .sprite_botmid(f3), .sprite_bottom(f4), .y_placement(y),
    .background_out(sprite_mover_7_background_out), .out(sprite_mover_7_out), .save_to_background(save),
    .delete_row(delete), .full_row_in(sprite_mover_6_out), .row_out(row_3),
    .full_count_in(sprite_mover_6_full_count_out), .full_count_out(sprite_mover_7_full_count_out),
    .erase(restart));
  sprite_mover sprite_mover_8 (
    .line_in(sprite_mover_7_next_line), .next_line(sprite_mover_8_next_line), .sprite_top(f1),
    .sprite_topmid(f2), .sprite_botmid(f3), .sprite_bottom(f4), .y_placement(y),
    .background_out(sprite_mover_8_background_out), .out(sprite_mover_8_out), .save_to_background(save),
    .delete_row(delete), .full_row_in(sprite_mover_7_out), .row_out(row_4),
    .full_count_in(sprite_mover_7_full_count_out), .full_count_out(sprite_mover_8_full_count_out),
    .erase(restart));
  sprite_mover sprite_mover_9 (
    .line_in(sprite_mover_8_next_line), .next_line(sprite_mover_9_next_line), .sprite_top(f1),
    .sprite_topmid(f2), .sprite_botmid(f3), .sprite_bottom(f4), .y_placement(y),
    .background_out(sprite_mover_9_background_out), .out(sprite_mover_9_out), .save_to_background(save),
    .delete_row(delete), .full_row_in(sprite_mover_8_out), .row_out(row_5),
    .full_count_in(sprite_mover_8_full_count_out), .full_count_out(sprite_mover_9_full_count_out),
    .erase(restart));
  sprite_mover sprite_mover_10 (
    .line_in(sprite_mover_9_next_line), .next_line(sprite_mover_10_next_line), .sprite_top(f1),
    .sprite_topmid(f2), .sprite_botmid(f3), .sprite_bottom(f4), .y_placement(y),
    .background_out(sprite_mover_10_background_out), .out(sprite_mover_10_out), .save_to_background(save),
    .delete_row(delete), .full_row_in(sprite_mover_9_out), .row_out(row_6),
    .full_count_in(sprite_mover_9_full_count_out), .full_count_out(sprite_mover_10_full_count_out),
    .erase(restart));
  sprite_mover sprite_mover_11 (
    .line_in(sprite_mover_10_next_line), .next_line(sprite_mover_11_next_line), .sprite_top(f1),
    .sprite_topmid(f2), .sprite_botmid(f3), .sprite_bottom(f4), .y_placement(y),
    .background_out(sprite_mover_11_background_out), .out(sprite_mover_11_out), .save_to_background(save),
    .delete_row(delete), .full_row_in(sprite_mover_10_out), .row_out(row_7),
    .full_count_in(sprite_mover_10_full_count_out), .full_count_out(sprite_mover_11_full_count_out),
    .erase(restart));
  sprite_mover sprite_mover_12 (
    .line_in(sprite_mover_11_next_line), .next_line(sprite_mover_12_next_line), .sprite_top(f1),
    .sprite_topmid(f2), .sprite_botmid(f3), .sprite_bottom(f4), .y_placement(y),
    .background_out(sprite_mover_12_background_out), .out(sprite_mover_12_out), .save_to_background(save),
    .delete_row(delete), .full_row_in(sprite_mover_11_out), .row_out(row_8),
    .full_count_in(sprite_mover_11_full_count_out), .full_count_out(sprite_mover_12_full_count_out),
    .erase(restart));
  sprite_mover sprite_mover_13 (
    .line_in(sprite_mover_12_next_line), .next_line(sprite_mover_13_next_line), .sprite_top(f1),
    .sprite_topmid(f2), .sprite_botmid(f3), .sprite_bottom(f4), .y_placement(y),
    .background_out(sprite_mover_13_background_out), .out(sprite_mover_13_out), .save_to_background(save),
    .delete_row(delete), .full_row_in(sprite_mover_12_out), .row_out(row_9),
    .full_count_in(sprite_mover_12_full_count_out), .full_count_out(sprite_mover_13_full_count_out),
    .erase(restart));
  sprite_mover sprite_mover_14 (
    .line_in(sprite_mover_13_next_line), .next_line(sprite_mover_14_next_line), .sprite_top(f1),
    .sprite_topmid(f2), .sprite_botmid(f3), .sprite_bottom(f4), .y_placement(y),
    .background_out(sprite_mover_14_background_out), .out(sprite_mover_14_out), .save_to_background(save),
    .delete_row(delete), .full_row_in(sprite_mover_13_out), .row_out(row_10),
    .full_count_in(sprite_mover_13_full_count_out), .full_count_out(sprite_mover_14_full_count_out),
    .erase(restart));
  sprite_mover sprite_mover_15 (
    .line_in(sprite_mover_14_next_line), .next_line(sprite_mover_15_next_line), .sprite_top(f1),
    .sprite_topmid(f2), .sprite_botmid(f3), .sprite_bottom(f4), .y_placement(y),
    .background_out(sprite_mover_15_background_out), .out(sprite_mover_15_out), .save_to_background(save),
    .delete_row(delete), .full_row_in(sprite_mover_14_out), .row_out(row_11),
    .full_count_in(sprite_mover_14_full_count_out), .full_count_out(sprite_mover_15_full_count_out),
    .erase(restart));
  sprite_mover sprite_mover_16 (
    .line_in(sprite_mover_15_next_line), .next_line(sprite_mover_16_next_line), .sprite_top(f1),
    .sprite_topmid(f2), .sprite_botmid(f3), .sprite_bottom(f4), .y_placement(y),
    .background_out(sprite_mover_16_background_out), .out(sprite_mover_16_out), .save_to_background(save),
    .delete_row(delete), .full_row_in(sprite_mover_15_out), .row_out(row_12),
    .full_count_in(sprite_mover_15_full_count_out), .full_count_out(sprite_mover_16_full_count_out),
    .erase(restart));
  sprite_mover sprite_mover_17 (
    .line_in(sprite_mover_16_next_line), .next_line(sprite_mover_17_next_line), .sprite_top(f1),
    .sprite_topmid(f2), .sprite_botmid(f3), .sprite_bottom(f4), .y_placement(y),
    .background_out(sprite_mover_17_background_out), .out(sprite_mover_17_out), .save_to_background(save),
    .delete_row(delete), .full_row_in(sprite_mover_16_out), .row_out(row_13),
    .full_count_in(sprite_mover_16_full_count_out), .full_count_out(sprite_mover_17_full_count_out),
    .erase(restart));
  sprite_mover sprite_mover_18 (
    .line_in(sprite_mover_17_next_line), .next_line(sprite_mover_18_next_line), .sprite_top(f1),
    .sprite_topmid(f2), .sprite_botmid(f3), .sprite_bottom(f4), .y_placement(y),
    .background_out(sprite_mover_18_background_out), .out(sprite_mover_18_out), .save_to_background(save),
    .delete_row(delete), .full_row_in(sprite_mover_17_out), .row_out(row_14),
    .full_count_in(sprite_mover_17_full_count_out), .full_count_out(sprite_mover_18_full_count_out),
    .erase(restart));
  sprite_mover sprite_mover_19 (
    .line_in(sprite_mover_18_next_line), .next_line(sprite_mover_19_next_line), .sprite_top(f1),
    .sprite_topmid(f2), .sprite_botmid(f3), .sprite_bottom(f4), .y_placement(y),
    .background_out(sprite_mover_19_background_out), .out(sprite_mover_19_out), .save_to_background(save),
    .delete_row(delete), .full_row_in(sprite_mover_18_out), .row_out(row_15),
    .full_count_in(sprite_mover_18_full_count_out), .full_count_out(sprite_mover_19_full_count_out),
    .erase(restart));
  sprite_mover sprite_mover_20 (
    .line_in(sprite_mover_19_next_line), .next_line(sprite_mover_20_next_line), .sprite_top(f1),
    .sprite_topmid(f2), .sprite_botmid(f3), .sprite_bottom(f4), .y_placement(y),
    .background_out(sprite_mover_20_background_out), .out(sprite_mover_20_out), .save_to_background(save),
    .delete_row(delete), .full_row_in(sprite_mover_19_out), .row_out(row_16),
    .full_count_in(sprite_mover_19_full_count_out), .full_count_out(sprite_mover_20_full_count_out),
    .erase(restart));
  sprite_mover sprite_mover_21 (
    .line_in(sprite_mover_20_next_line), .next_line(sprite_mover_21_next_line), .sprite_top(f1),
    .sprite_topmid(f2), .sprite_botmid(f3), .sprite_bottom(f4), .y_placement(y),
    .background_out(sprite_mover_21_background_out), .out(sprite_mover_21_out), .save_to_background(save),
    .delete_row(delete), .full_row_in(sprite_mover_20_out), .row_out(row_17),
    .full_count_in(sprite_mover_20_full_count_out), .full_count_out(sprite_mover_21_full_count_out),
    .erase(restart));
  sprite_mover sprite_mover_22 (
    .line_in(sprite_mover_21_next_line), .next_line(sprite_mover_22_next_line), .sprite_top(f1),
    .sprite_topmid(f2), .sprite_botmid(f3), .sprite_bottom(f4), .y_placement(y),
    .background_out(sprite_mover_22_background_out), .out(sprite_mover_22_out), .save_to_background(save),
    .delete_row(delete), .full_row_in(sprite_mover_21_out), .row_out(row_18),
    .full_count_in(sprite_mover_21_full_count_out), .full_count_out(sprite_mover_22_full_count_out),
    .erase(restart));
  sprite_mover sprite_mover_23 (
    .line_in(sprite_mover_22_next_line), .next_line(sprite_mover_23_next_line), .sprite_top(f1),
    .sprite_topmid(f2), .sprite_botmid(f3), .sprite_bottom(f4), .y_placement(y),
    .background_out(sprite_mover_23_background_out), .out(sprite_mover_23_out), .save_to_background(save),
    .delete_row(delete), .full_row_in(sprite_mover_22_out), .row_out(row_19),
    .full_count_in(sprite_mover_22_full_count_out), .full_count_out(sprite_mover_23_full_count_out),
    .erase(restart));
  sprite_mover sprite_mover_24 (
    .line_in(sprite_mover_23_next_line), .next_line(sprite_mover_24_next_line), .sprite_top(f1),
    .sprite_topmid(f2), .sprite_botmid(f3), .sprite_bottom(f4), .y_placement(y), .background_out(l20_b),
    .out(sprite_mover_24_out), .save_to_background(save), .delete_row(delete),
    .full_row_in(sprite_mover_23_out), .row_out(row_20), .full_count_in(sprite_mover_23_full_count_out),
    .full_count_out(sprite_mover_24_full_count_out), .erase(restart));
  sprite_mover sprite_mover_25 (
    .line_in(sprite_mover_24_next_line), .next_line(sprite_mover_25_next_line), .sprite_top(f1),
    .sprite_topmid(f2), .sprite_botmid(f3), .sprite_bottom(f4), .y_placement(y), .out(sprite_mover_25_out),
    .save_to_background(save), .delete_row(delete), .full_row_in(sprite_mover_24_out),
    .full_count_in(sprite_mover_24_full_count_out), .full_count_out(sprite_mover_25_full_count_out),
    .erase(restart));  // open: background_out, row_out
  sprite_mover sprite_mover_26 (
    .line_in(sprite_mover_25_next_line), .next_line(sprite_mover_26_next_line), .sprite_top(f1),
    .sprite_topmid(f2), .sprite_botmid(f3), .sprite_bottom(f4), .y_placement(y), .out(sprite_mover_26_out),
    .save_to_background(save), .delete_row(delete), .full_row_in(sprite_mover_25_out),
    .full_count_in(sprite_mover_25_full_count_out), .full_count_out(sprite_mover_26_full_count_out),
    .erase(restart));  // open: background_out, row_out
  sprite_mover sprite_mover_27 (
    .line_in(sprite_mover_26_next_line), .sprite_top(f1), .sprite_topmid(f2), .sprite_botmid(f3),
    .sprite_bottom(f4), .y_placement(y), .save_to_background(save), .delete_row(delete),
    .full_row_in(sprite_mover_26_out), .full_count_in(sprite_mover_26_full_count_out),
    .full_count_out(full_counter), .erase(restart));  // open: next_line, background_out, out, row_out
  or or_4 (side_move, and_1_out, and_2_out);
  and and_1 (and_1_out, ~collision_left, move_left);  // AND_Gate
  not not_1 (no_placement, comparator_1_eq);
  Comparator #(.width(10)) comparator_1 (.a(l1_b), .b({10{1'b0}}), .eq(comparator_1_eq));  // open: gt, lt
  and and_2 (and_2_out, move_right, ~collision_right);  // AND_Gate
  assign bit_extender_1_out = {{12{1'b0}}, curr_figure[3:0]};  // Bit_Extender bit_extender_1
  Shifter #(.width(16)) shifter_1 (.in(bit_extender_1_out), .\dist (x), .out(shifter_1_out));
  assign bit_extender_2_out = {{12{1'b0}}, curr_figure[7:4]};  // Bit_Extender bit_extender_2
  Shifter #(.width(16)) shifter_2 (.in(bit_extender_2_out), .\dist (x), .out(shifter_2_out));
  assign bit_extender_3_out = {{12{1'b0}}, curr_figure[11:8]};  // Bit_Extender bit_extender_3
  Shifter #(.width(16)) shifter_3 (.in(bit_extender_3_out), .\dist (x), .out(shifter_3_out));
  assign bit_extender_4_out = {{12{1'b0}}, curr_figure[15:12]};  // Bit_Extender bit_extender_4
  Shifter #(.width(16)) shifter_4 (.in(bit_extender_4_out), .\dist (x), .out(shifter_4_out));
  Multiplexer #(.width(4)) multiplexer_1 (
    .in0(l_x), .in1(r_x), .out(multiplexer_1_out), .sel(move_right), .en(side_move));
  Multiplexer #(.width(4), .enable("false")) multiplexer_2 (
    .in0(multiplexer_1_out), .in1(4'b0111), .out(multiplexer_2_out), .sel(and_3_out));
  and and_3 (and_3_out, ~side_move, spawn);  // AND_Gate
  Adder #(.width(4)) adder_1 (.a(x), .b(4'b0001), .out(adder_1_out));  // open: cin, cout
  Subtractor #(.width(4)) subtractor_1 (.a(x), .b(4'b0001), .out(subtractor_1_out));  // open: bin, bout
  and and_4 (and_4_out, collision_down, ~pause_out);  // AND_Gate
  D_Flip_Flop d_ff_1 (.clk(and_4_out), .D(1'b1), .Q(save), .reset(not_3_out));  // open: Qn, preset, en
  not not_2 (not_2_out, save);
  not not_3 (not_3_out, not_5_out);
  not not_4 (not_4_out, not_2_out);
  not not_5 (not_5_out, not_7_out);
  not not_6 (not_6_out, not_4_out);
  not not_7 (not_7_out, not_6_out);
  Shifter #(.width(16), .shift("lr")) shifter_5 (.in(shifter_1_out), .\dist (4'b0100), .out(shifter_5_out));
  Shifter #(.width(16), .shift("lr")) shifter_6 (.in(shifter_2_out), .\dist (4'b0100), .out(shifter_6_out));
  Shifter #(.width(16), .shift("lr")) shifter_7 (.in(shifter_3_out), .\dist (4'b0100), .out(shifter_7_out));
  Shifter #(.width(16), .shift("lr")) shifter_8 (.in(shifter_4_out), .\dist (4'b0100), .out(shifter_8_out));
  not not_8 (not_8_out, pause_out);
  or or_5 (or_5_out, spawn, side_move);
  Register #(.width(4)) register_1 (.D(adder_1_out), .Q(l_x), .clk(or_6_out));  // open: en, clr
  or or_6 (or_6_out, spawn, side_move);
  Register #(.width(4)) register_2 (.D(subtractor_1_out), .Q(r_x), .clk(or_7_out));  // open: en, clr
  or or_7 (or_7_out, spawn, side_move);
  or or_8 (or_8_out, save, restart);
  Bit_Extender #(.in_width(16), .out_width(10)) bit_extender_5 (.in(shifter_5_out), .out(f1));
  Bit_Extender #(.in_width(16), .out_width(10)) bit_extender_6 (.in(shifter_6_out), .out(f2));
  Bit_Extender #(.in_width(16), .out_width(10)) bit_extender_7 (.in(shifter_7_out), .out(f3));
  Bit_Extender #(.in_width(16), .out_width(10)) bit_extender_8 (.in(shifter_8_out), .out(f4));
  assign or_9_out = f4 | f3 | f2 | f1;  // OR_Gate or_9, 10 bits wide
  Register #(.width(4), .trigger("falling")) register_3 (
    .D(multiplexer_2_out), .en(not_8_out), .Q(x), .clk(or_5_out));  // open: clr
  D_Flip_Flop #(.trigger("falling")) d_ff_2 (
    .clk(or_8_out), .D(1'b1), .Q(spawn), .reset(not_10_out));  // open: Qn, preset, en
  not not_9 (not_9_out, spawn);
  not not_10 (not_10_out, not_12_out);
  not not_11 (not_11_out, not_9_out);
  not not_12 (not_12_out, not_14_out);
  not not_13 (not_13_out, not_11_out);
  not not_14 (not_14_out, not_13_out);
  // Probe on f1
  // Probe on f2
  // Probe on f3
  // Probe on f4
  Pull_Resistor pull_resistor_4 (.node(right_bord));
  Pull_Resistor pull_resistor_5 (.node(left_bord));
  buf buffer_1 (left_bord, or_9_out[9]);
  buf buffer_2 (right_bord, or_9_out[0]);
  get_figure get_figure_1 (
    .get_next(get_next), .get_first(not_16_out), .curr_figure(curr_figure), .next_figure(next_figure),
    .rotate(rotate), .spawn(spawn_new));
  not not_15 (not_15_out, restart);
  not not_16 (not_16_out, not_15_out);
  and and_5 (and_5_out, game_clk, ~or_10_out, ~collision_down);  // AND_Gate
  or or_10 (or_10_out, move_right, move_left, rotate);
  D_Flip_Flop #(.trigger("falling")) d_ff_3 (
    .clk(spawn), .D(1'b1), .Q(get_next), .reset(not_18_out));  // open: Qn, preset, en
  not not_17 (not_17_out, get_next);
  not not_18 (not_18_out, not_20_out);
  not not_19 (not_19_out, not_17_out);
  not not_20 (not_20_out, not_22_out);
  not not_21 (not_21_out, not_19_out);
  not not_22 (not_22_out, not_21_out);
  // Probe on curr_figure
  Counter #(.max('h1f), .trigger("falling")) counter_1 (
    .Q(y), .clk(and_5_out), .clr(spawn));  // open: load, D, count, carry
  Counter #(.max('haf)) counter_2 (.carry(game_clk), .clk(clk));  // open: load, D, count, Q, clr
  next_field next_field_1 (
    .next_figure(next_figure), .line_1(next_1), .line_2(next_2), .line_3(next_3), .line_4(next_4),
    .line_5(next_5), .line_6(next_6));
  assign xor_1_out = row_20 ^ l20_b;  // XOR_Gate xor_1, 10 bits wide
  Comparator #(.width(10)) comparator_2 (.a(xor_1_out), .b({10{1'b0}}), .eq(comparator_2_eq));  // open: gt, lt
  proc proc_1 (.pause(pause_out), .restart(restart), .game_over(game_over), .out_4(clk));
  T_Flip_Flop t_ff_1 (.clk(pause), .T(pause), .Q(pause_out), .en(not_23_out));  // open: Qn, preset, reset
  not not_23 (not_23_out, game_over);
  D_Flip_Flop d_ff_4 (.clk(no_placement), .D(1'b1), .Q(game_over), .reset(restart));  // open: Qn, preset, en
  Subtractor subtractor_2 (.a(full_counter), .b(8'h1), .out(subtractor_2_out));  // open: bin, bout
  not not_24 (deletion, comparator_3_eq);
  Comparator #(.mode("unsigned")) comparator_3 (.a(full_counter), .b({8{1'b0}}), .eq(comparator_3_eq));  // open: gt, lt
  Multiplexer #(.width(32), .enable("false")) multiplexer_3 (
    .in0(score), .in1(score_temp), .out(multiplexer_3_out), .sel(deletion));
  not not_25 (bottom, comparator_2_eq);
  Bit_Extender #(.out_width(2)) bit_extender_9 (.in(subtractor_2_out), .out(counter));
  D_Flip_Flop d_ff_5 (.clk(deletion), .D(1'b1), .Q(score_en), .reset(clk));  // open: Qn, preset, en
  and and_6 (delete, deletion, clk);
  Register #(.width(32), .trigger("falling")) register_4 (
    .D(multiplexer_3_out), .Q(score), .clk(score_en), .clr(restart));  // open: en
  Multiplexer #(.select(2), .width(32)) multiplexer_4 (
    .in0(32'h64), .in1(32'h12c), .in2(32'h2bc), .in3(32'h5dc), .out(multiplexer_4_out), .sel(counter),
    .en(deletion));
  Adder #(.width(32)) adder_2 (.a(score), .b(multiplexer_4_out), .out(score_temp));  // open: cin, cout

  // Other names for the same wires on the sheet: sprite_top[3:0] = curr_figure[3:0];
  //   sprite_topmid[3:0] = curr_figure[7:4]; sprite_botmid[3:0] = curr_figure[11:8];
  //   sprite_bot[3:0] = curr_figure[15:12]; l1[9:0] = row_1; l2[9:0] = row_2; l3[9:0] = row_3; l4[9:0] = row_4;
  //   l5[9:0] = row_5; l6[9:0] = row_6; l7[9:0] = row_7; l8[9:0] = row_8; l9[9:0] = row_9; l10[9:0] = row_10;
  //   l11[9:0] = row_11; l12[9:0] = row_12; l13[9:0] = row_13; l14[9:0] = row_14; l15[9:0] = row_15;
  //   l16[9:0] = row_16; l17[9:0] = row_17; l18[9:0] = row_18; l19[9:0] = row_19; l20[9:0] = row_20; left = move_left;
  //   next1[7:0] = next_1; next2[7:0] = next_2; next3[7:0] = next_3; next4[7:0] = next_4; next5[7:0] = next_5;
  //   next6[7:0] = next_6; pause_state = pause_out; right = move_right

  // Notes on the sheet:
  //   OUTPUTS
  //   INPUTS
  //   MAIN CONTROLLER
  //   CONST-TO-SPRITE CONSTRUCTOR
  //   SIDE MOVER
  //   SPAWN CONTROLLER
  //   buffer_1 drives only 1 and floats otherwise
  //   buffer_2 drives only 1 and floats otherwise
  //   DOWN MOVER
  //   1 row score
  //   2 row score
  //   3 row score
  //   4 row score
  //   CLOCK CONTROLLER
  //   DELETION CONTROLLER
  //   SCORE COUNTER
endmodule

// sprite ctor
module get_figure (
  input  get_next,
  input  get_first,
  input  rotate,
  output [15:0] curr_figure,
  output [15:0] next_figure,
  output spawn
);

  wire get_n, not_1_out, not_2_out, not_3_out, not_4_out, not_5_out, not_6_out, not_7_out, not_8_out,
       or_1_out, or_2_out, or_3_out, or_4_out, or_5_out;
  wire [1:0] counter_1_q, counter_2_q, counter_3_q, counter_4_q, counter_5_q, counter_6_q, counter_7_q;
  wire [2:0] gened_num, multiplexer_10_out, prev_gened, register_2_q;
  wire [15:0] I_pos, J_pos, L_pos, multiplexer_5_out, multiplexer_6_out, multiplexer_9_out, O_pos,
       rotated_curr, S_pos, T_pos, Z_pos;

  Multiplexer #(.select(2), .width(16), .enable("false")) multiplexer_1 (
    .in0(16'hf0), .in1(16'h2222), .in2(16'hf00), .in3(16'h4444), .out(I_pos), .sel(counter_1_q));
  Counter #(.width(2), .max('h3)) counter_1 (
    .Q(counter_1_q), .clk(rotate), .clr(get_next));  // open: load, D, count, carry
  Multiplexer #(.select(2), .width(16), .enable("false")) multiplexer_2 (
    .in0(16'h6c), .in1(16'h462), .in2(16'h6c0), .in3(16'h8c4), .out(Z_pos), .sel(counter_2_q));
  Counter #(.width(2), .max('h3)) counter_2 (
    .Q(counter_2_q), .clk(rotate), .clr(get_next));  // open: load, D, count, carry
  DotMatrix #(.inputtype("row"), .matrixcols(4), .matrixrows(4)) dotmatrix_1 (
    .row0(curr_figure[3:0]), .row1(curr_figure[7:4]), .row2(curr_figure[11:8]), .row3(curr_figure[15:12]));
  Counter #(.width(2), .max('h3)) counter_3 (
    .Q(counter_3_q), .clk(rotate), .clr(get_next));  // open: load, D, count, carry
  Counter #(.width(2), .max('h3)) counter_4 (
    .Q(counter_4_q), .clk(rotate), .clr(get_next));  // open: load, D, count, carry
  Multiplexer #(.select(2), .width(16), .enable("false")) multiplexer_3 (
    .in0(16'he4), .in1(16'h464), .in2(16'h4e0), .in3(16'h4c4), .out(T_pos), .sel(counter_3_q));
  Multiplexer #(.select(2), .width(16), .enable("false")) multiplexer_4 (
    .in0(16'he8), .in1(16'h446), .in2(16'h2e0), .in3(16'hc44), .out(J_pos), .sel(counter_4_q));
  or or_1 (or_1_out, get_first, get_next);
  Random #(.width(3), .trigger("falling")) random_1 (.clk(or_1_out), .out(gened_num));  // open: next, clr
  Multiplexer #(.select(3), .width(16), .enable("false")) multiplexer_5 (
    .in0(16'hf0), .in1(16'hf0), .in2(16'he4), .in3(16'h66), .in4(16'hc6), .in5(16'h6c), .in6(16'he8),
    .in7(16'he2), .out(multiplexer_5_out), .sel(gened_num));
  Register #(.width(16)) register_1 (.D(multiplexer_5_out), .Q(next_figure), .clk(not_1_out));  // open: en, clr
  not not_1 (not_1_out, or_2_out);
  or or_2 (or_2_out, get_next, get_n, get_first);
  Multiplexer #(.width(16), .enable("false")) multiplexer_6 (
    .in0(next_figure), .in1({16{1'b0}}), .out(multiplexer_6_out), .sel(get_first));
  Multiplexer #(.select(2), .width(16), .enable("false")) multiplexer_7 (
    .in0(16'h66), .in1(16'h66), .in2(16'h66), .in3(16'h66), .out(O_pos), .sel(counter_5_q));
  Counter #(.width(2), .max('h3)) counter_5 (
    .Q(counter_5_q), .clk(rotate), .clr(get_next));  // open: load, D, count, carry
  Multiplexer #(.select(2), .width(16), .enable("false")) multiplexer_8 (
    .in0(16'he2), .in1(16'h644), .in2(16'h8e0), .in3(16'h44c), .out(L_pos), .sel(counter_6_q));
  Counter #(.width(2), .max('h3)) counter_6 (
    .Q(counter_6_q), .clk(rotate), .clr(get_next));  // open: load, D, count, carry
  Register #(.width(3)) register_2 (.D(gened_num), .Q(register_2_q), .clk(not_2_out));  // open: en, clr
  not not_2 (not_2_out, or_3_out);
  or or_3 (or_3_out, get_next, get_n, get_first);
  Register #(.width(16)) register_3 (.D(multiplexer_9_out), .Q(curr_figure), .clk(not_3_out));  // open: en, clr
  Multiplexer #(.width(16), .enable("false")) multiplexer_9 (
    .in0(multiplexer_6_out), .in1(rotated_curr), .out(multiplexer_9_out), .sel(rotate));
  not not_3 (not_3_out, or_4_out);
  or or_4 (or_4_out, get_next, get_n, get_first, rotate);
  Register #(.width(3)) register_4 (.D(multiplexer_10_out), .Q(prev_gened), .clk(not_4_out));  // open: en, clr
  Multiplexer #(.width(3), .enable("false")) multiplexer_10 (
    .in0(register_2_q), .in1(3'b000), .out(multiplexer_10_out), .sel(get_first));
  not not_4 (not_4_out, or_5_out);
  or or_5 (or_5_out, get_next, get_n, get_first);
  Multiplexer #(.select(2), .width(16), .enable("false")) multiplexer_11 (
    .in0(16'hc6), .in1(16'h264), .in2(16'hc60), .in3(16'h4c8), .out(S_pos), .sel(counter_7_q));
  Counter #(.width(2), .max('h3)) counter_7 (
    .Q(counter_7_q), .clk(rotate), .clr(get_next));  // open: load, D, count, carry
  or or_6 (spawn, get_n, get_first);
  Multiplexer #(.select(3), .width(16), .enable("false")) multiplexer_12 (
    .in0(I_pos), .in1(I_pos), .in2(T_pos), .in3(O_pos), .in4(S_pos), .in5(Z_pos), .in6(J_pos), .in7(L_pos),
    .out(rotated_curr), .sel(prev_gened));
  D_Flip_Flop #(.trigger("falling")) d_ff_1 (
    .clk(get_first), .D(1'b1), .Q(get_n), .reset(not_8_out));  // open: Qn, preset, en
  not not_5 (not_5_out, get_n);
  not not_6 (not_6_out, not_5_out);
  not not_7 (not_7_out, not_6_out);
  not not_8 (not_8_out, not_7_out);

  // Notes on the sheet:
  //   FIGURE SET
  //   0
  //   INPUTS
  //   OUTPUTS
  //   90
  //   ROTATION SETS
  //   180
  //   270
  //   FIGURE ROTATION CONTROLLER
  //   NUM GEN
  //   Replace with custom random chip
  //   SPRITE CONTROLLER
endmodule

// mover
module sprite_mover (
  input  [7:0] line_in,
  input  [7:0] y_placement,
  input  [9:0] sprite_top,
  input  [9:0] sprite_topmid,
  input  [9:0] sprite_botmid,
  input  [9:0] sprite_bottom,
  input  [9:0] full_row_in,
  input  [7:0] full_count_in,
  input  save_to_background,
  input  delete_row,
  input  erase,
  output [7:0] next_line,
  output [9:0] background_out,
  output [9:0] out,
  output [9:0] row_out,
  output [7:0] full_count_out
);

  wire and_1_out, and_2_out, comparator_1_eq, comparator_2_eq, comparator_3_lt, comparator_4_lt, or_2_out;
  wire [1:0] bit_extender_1_out;
  wire [7:0] subtractor_1_out;
  wire [9:0] check, multiplexer_2_out;

  Adder adder_1 (.a(line_in), .b(8'h1), .out(next_line));  // open: cin, cout
  Comparator #(.width(10)) comparator_1 (.a(background_out), .b({10{1'b1}}), .eq(comparator_1_eq));  // open: gt, lt
  Adder adder_2 (.a(full_count_in), .b({8{1'b0}}), .out(full_count_out), .cin(comparator_1_eq));  // open: cout
  Subtractor subtractor_1 (.a(line_in), .b(y_placement), .out(subtractor_1_out));  // open: bin, bout
  Bit_Extender #(.out_width(2)) bit_extender_1 (.in(subtractor_1_out), .out(bit_extender_1_out));
  assign row_out = check | background_out;  // OR_Gate or_1, 10 bits wide
  Comparator comparator_2 (.a(full_count_in), .b({8{1'b0}}), .eq(comparator_2_eq));  // open: gt, lt
  Comparator comparator_3 (.a({8{1'b1}}), .b(subtractor_1_out), .lt(comparator_3_lt));  // open: gt, eq
  Comparator comparator_4 (.a(subtractor_1_out), .b(8'h4), .lt(comparator_4_lt));  // open: gt, eq
  Multiplexer #(.select(2), .width(10), .disabled(0)) multiplexer_1 (
    .in0(sprite_top), .in1(sprite_topmid), .in2(sprite_botmid), .in3(sprite_bottom), .out(check),
    .sel(bit_extender_1_out), .en(and_2_out));
  Multiplexer #(.width(10), .enable("false")) multiplexer_2 (
    .in0(row_out), .in1(full_row_in), .out(multiplexer_2_out), .sel(and_1_out));
  or or_2 (or_2_out, and_1_out, save_to_background);
  and and_1 (and_1_out, comparator_2_eq, delete_row);
  and and_2 (and_2_out, comparator_3_lt, comparator_4_lt);
  Register #(.width(10), .trigger("falling")) register_1 (
    .D(multiplexer_2_out), .Q(background_out), .clk(or_2_out), .clr(erase));  // open: en

  assign out = background_out;

  // Other names for the same wires on the sheet: count_in[7:0] = full_count_in; count_out[7:0] = full_count_out;
  //   delete = delete_row; f1[9:0] = sprite_top; f2[9:0] = sprite_topmid; f3[9:0] = sprite_botmid;
  //   f4[9:0] = sprite_bottom; row_in[9:0] = full_row_in; save = save_to_background; y[7:0] = y_placement

  // Notes on the sheet:
  //   line_in: pull=down
  //   delete_row: pull=down
  //   full_row_in: pull=down
  //   full_count_in: pull=down
  //   y_placement: pull=down
  //   INPUTS
  //   OUTPUTS
  //   NEXT LINE
  //   FULL LINES COUNTER
  //   FIGURE LINE PLACEMENT
  //   SAVE AND DELETE
endmodule

module collision (
  input  [7:0] line_in,
  input  [7:0] y_placement,
  input  [9:0] sprite_top,
  input  [9:0] sprite_topmid,
  input  [9:0] sprite_botmid,
  input  [9:0] sprite_bottom,
  input  [9:0] background_row,
  output [7:0] next_line,
  output collision_left,
  output collision_right,
  output collision_down
);

  wire and_2_out, and_5_out, comparator_1_lt, comparator_2_lt, comparator_3_eq, comparator_4_lt,
       comparator_5_lt, comparator_6_eq, comparator_7_eq;
  wire [1:0] bit_extender_1_out, bit_extender_2_out;
  wire [7:0] down_line, subtractor_1_out, subtractor_2_out;
  wire [9:0] and_1_out, and_3_out, and_4_out, bot_check, shifter_1_out, shifter_2_out, side_check;

  Subtractor subtractor_1 (.a(down_line), .b(y_placement), .out(subtractor_1_out));  // open: bin, bout
  assign and_1_out = bot_check & background_row;  // AND_Gate and_1, 10 bits wide
  Adder adder_1 (.a(line_in), .b(8'h1), .out(next_line));  // open: cin, cout
  Adder adder_2 (.a(next_line), .b(8'h2), .out(down_line));  // open: cin, cout
  Comparator comparator_1 (.a({8{1'b1}}), .b(subtractor_1_out), .lt(comparator_1_lt));  // open: gt, eq
  Comparator comparator_2 (.a(subtractor_1_out), .b(8'h4), .lt(comparator_2_lt));  // open: gt, eq
  Bit_Extender #(.out_width(2)) bit_extender_1 (.in(subtractor_1_out), .out(bit_extender_1_out));
  Comparator #(.width(10)) comparator_3 (.a(and_1_out), .b({10{1'b0}}), .eq(comparator_3_eq));  // open: gt, lt
  not not_1 (collision_down, comparator_3_eq);
  and and_2 (and_2_out, comparator_1_lt, comparator_2_lt);
  Multiplexer #(.select(2), .width(10), .disabled(0)) multiplexer_1 (
    .in0(sprite_top), .in1(sprite_topmid), .in2(sprite_botmid), .in3(sprite_bottom), .out(bot_check),
    .sel(bit_extender_1_out), .en(and_2_out));
  Subtractor subtractor_2 (.a(line_in), .b(y_placement), .out(subtractor_2_out));  // open: bin, bout
  Shifter #(.width(10)) shifter_1 (.in(side_check), .\dist (4'b0001), .out(shifter_1_out));
  Shifter #(.width(10), .shift("lr")) shifter_2 (.in(side_check), .\dist (4'b0001), .out(shifter_2_out));
  Comparator comparator_4 (.a({8{1'b1}}), .b(subtractor_2_out), .lt(comparator_4_lt));  // open: gt, eq
  Comparator comparator_5 (.a(subtractor_2_out), .b(8'h4), .lt(comparator_5_lt));  // open: gt, eq
  Bit_Extender #(.out_width(2)) bit_extender_2 (.in(subtractor_2_out), .out(bit_extender_2_out));
  assign and_3_out = shifter_1_out & background_row;  // AND_Gate and_3, 10 bits wide
  assign and_4_out = shifter_2_out & background_row;  // AND_Gate and_4, 10 bits wide
  and and_5 (and_5_out, comparator_4_lt, comparator_5_lt);
  Multiplexer #(.select(2), .width(10), .disabled(0)) multiplexer_2 (
    .in0(sprite_top), .in1(sprite_topmid), .in2(sprite_botmid), .in3(sprite_bottom), .out(side_check),
    .sel(bit_extender_2_out), .en(and_5_out));
  Comparator #(.width(10)) comparator_6 (.a(and_3_out), .b({10{1'b0}}), .eq(comparator_6_eq));  // open: gt, lt
  not not_2 (collision_left, comparator_6_eq);
  not not_3 (collision_right, comparator_7_eq);
  Comparator #(.width(10)) comparator_7 (.a(and_4_out), .b({10{1'b0}}), .eq(comparator_7_eq));  // open: gt, lt

  // Other names for the same wires on the sheet: background[9:0] = background_row; down = collision_down;
  //   f1[9:0] = sprite_top; f2[9:0] = sprite_topmid; f3[9:0] = sprite_botmid; f4[9:0] = sprite_bottom;
  //   left = collision_left; right = collision_right; y[7:0] = y_placement

  // Notes on the sheet:
  //   line_in: pull=down
  //   y_placement: pull=down
  //   INPUTS
  //   OUTPUTS
  //   NEXT LINES
  //   BOTTOM COLLISION
  //   not_1 drives only 1 and floats otherwise
  //   SIDES COLLISION
  //   LEFT COLLISION
  //   RIGHT COLLISION
  //   not_2 drives only 1 and floats otherwise
  //   not_3 drives only 1 and floats otherwise
endmodule

// next-disp
module next_field (
  input  [15:0] next_figure,
  output [7:0] line_1,
  output [7:0] line_2,
  output [7:0] line_3,
  output [7:0] line_4,
  output [7:0] line_5,
  output [7:0] line_6
);


  assign line_1 = {8{1'b0}};
  assign line_2 = {8{1'b0}};
  assign line_3 = {2'b00, next_figure[3:0], 2'b00};
  assign line_4 = {2'b00, next_figure[7:4], 2'b00};
  assign line_5 = {8{1'b0}};
  assign line_6 = {8{1'b0}};

  // Other names for the same wires on the sheet: f1[3:0] = next_figure[3:0]; l3[5:2] = next_figure[3:0];
  //   next[15:0] = next_figure; f2[3:0] = next_figure[7:4]; l4[5:2] = next_figure[7:4]

  // Notes on the sheet:
  //   INPUTS
  //   OUTPUTS
endmodule
