// Logisim project tetris.circ as structural Verilog: 10 circuits, main circuit ui
module ui (
);

  wire button_1_out, button_2_out, button_3_out, button_4_out, button_5_out, field_1_game_over,
       field_1_pause_out;
  wire [3:0] field_1_score0, field_1_score1, field_1_score2, field_1_score3, field_1_score_1, field_1_score_2;
  wire [7:0] field_1_next_1, field_1_next_2, field_1_next_3, field_1_next_4, field_1_next_5, field_1_next_6;
  wire [9:0] field_1_row_1, field_1_row_2, field_1_row_3, field_1_row_4, field_1_row_5, field_1_row_6,
       field_1_row_7, field_1_row_8, field_1_row_9, field_1_row_10, field_1_row_11, field_1_row_12,
       field_1_row_13, field_1_row_14, field_1_row_15, field_1_row_16, field_1_row_17, field_1_row_18,
       field_1_row_19, field_1_row_20;

  Hex_Digit_Display hex_digit_display_1 (.value(field_1_score3));  // open: dp
  field field_1 (
    .row_1(field_1_row_1), .row_2(field_1_row_2), .row_3(field_1_row_3), .row_4(field_1_row_4),
    .row_5(field_1_row_5), .row_6(field_1_row_6), .row_7(field_1_row_7), .row_8(field_1_row_8),
    .row_9(field_1_row_9), .row_10(field_1_row_10), .row_11(field_1_row_11), .row_12(field_1_row_12),
    .row_13(field_1_row_13), .row_14(field_1_row_14), .row_15(field_1_row_15), .row_16(field_1_row_16),
    .row_17(field_1_row_17), .row_18(field_1_row_18), .row_19(field_1_row_19), .row_20(field_1_row_20),
    .next_1(field_1_next_1), .next_2(field_1_next_2), .next_3(field_1_next_3), .next_4(field_1_next_4),
    .next_5(field_1_next_5), .next_6(field_1_next_6), .pause_out(field_1_pause_out),
    .game_over(field_1_game_over), .move_left(button_1_out), .pause(button_4_out), .move_right(button_2_out),
    .restart(button_5_out), .rotate(button_3_out), .score0(field_1_score0), .score1(field_1_score1),
    .score2(field_1_score2), .score3(field_1_score3), .score_1(field_1_score_1), .score_2(field_1_score_2));
  DotMatrix #(.inputtype("row"), .matrixcols(10), .matrixrows(20)) dotmatrix_1 (
    .row0(field_1_row_1), .row1(field_1_row_2), .row2(field_1_row_3), .row3(field_1_row_4),
    .row4(field_1_row_5), .row5(field_1_row_6), .row6(field_1_row_7), .row7(field_1_row_8),
    .row8(field_1_row_9), .row9(field_1_row_10), .row10(field_1_row_11), .row11(field_1_row_12),
    .row12(field_1_row_13), .row13(field_1_row_14), .row14(field_1_row_15), .row15(field_1_row_16),
    .row16(field_1_row_17), .row17(field_1_row_18), .row18(field_1_row_19), .row19(field_1_row_20));
  Hex_Digit_Display hex_digit_display_2 (.value(field_1_score2));  // open: dp
  Hex_Digit_Display hex_digit_display_3 (.value(field_1_score1));  // open: dp
  Button button_1 (.out(button_1_out));
  Hex_Digit_Display hex_digit_display_4 (.value(field_1_score_1));  // open: dp
  Hex_Digit_Display hex_digit_display_5 (.value(field_1_score0));  // open: dp
  DotMatrix #(.inputtype("row"), .matrixcols(8), .matrixrows(6)) dotmatrix_2 (
    .row0(field_1_next_1), .row1(field_1_next_2), .row2(field_1_next_3), .row3(field_1_next_4),
    .row4(field_1_next_5), .row5(field_1_next_6));
  LED GAME_OVER (.in(field_1_game_over));
  LED ON_PAUSE (.in(field_1_pause_out));
  Button button_2 (.out(button_2_out));
  Button button_3 (.out(button_3_out));
  Hex_Digit_Display hex_digit_display_6 (.value(field_1_score_2));  // open: dp
  Button button_4 (.out(button_4_out));
  Button button_5 (.out(button_5_out));

  // Notes on the sheet:
  //   ROTATE
  //   LEFT
  //   SCORE
  //   NEXT
  //   TETRIS!
  //   RIGHT
  //   PAUSE
  //   RESTART
endmodule

module proc (
  input  pause,
  input  restart,
  input  game_over,
  input  [7:0] \input ,
  output [7:0] \output ,
  output clk,
  output \new 
);

  wire and_2_out, and_4_out, cdm_8_mark5_1_p1, cdm_8_mark5_1_p2, cdm_8_mark5_1_p4, cdm_8_mark5_1_p5,
       cdm_8_mark5_1_p6, cdm_8_mark5_1_p7, cdm_8_mark5_1_p8, cdm_8_mark5_1_p9, cdm_8_mark5_1_p10,
       clock_1_out, Code, Data, IOaddr, IOsel, not_1_out, not_2_out, proc, RAM, rd_wr_prime;
  wire [7:0] cdm_8_mark5_1_p13, cdm_8_mark5_1_p14, IOdat;
  wire [7:1] cdm_8_mark5_1_p12;

  Clock clock_1 (.out(clock_1_out));
  and and_1 (clk, ~pause, ~game_over, clock_1_out);  // AND_Gate
  // Probe on cdm_8_mark5_1_p5
  // Probe on cdm_8_mark5_1_p4
  // Probe on cdm_8_mark5_1_p2
  // Probe on cdm_8_mark5_1_p1
  // Probe on cdm_8_mark5_1_p6
  and and_2 (and_2_out, IOaddr, IOsel, rd_wr_prime);
  Counter #(.width(10), .max('h3ff)) counter_1 (.carry(proc), .clk(clk));  // open: load, D, count, Q, clr
  // Probe on cdm_8_mark5_1_p8
  // Probe on cdm_8_mark5_1_p7
  Decoder #(.disabled(0)) decoder_1 (.out0(Code), .out1(Data), .sel(cdm_8_mark5_1_p9), .en(cdm_8_mark5_1_p10));
  // CdM_8_mark5 cdm_8_mark5_1: pin names not known; wires that end beside it: cdm_8_mark5_1_p1, cdm_8_mark5_1_p2, proc, cdm_8_mark5_1_p4, cdm_8_mark5_1_p5, cdm_8_mark5_1_p6, cdm_8_mark5_1_p7, cdm_8_mark5_1_p8, cdm_8_mark5_1_p9, cdm_8_mark5_1_p10, rd_wr_prime, {cdm_8_mark5_1_p12, IOaddr}, cdm_8_mark5_1_p13, cdm_8_mark5_1_p14
  not not_1 (not_1_out, rd_wr_prime);
  assign IOdat = and_2_out ? \input  : 8'bz;  // Controlled_Buffer controlled_buffer_1
  assign IOdat = not_1_out ? cdm_8_mark5_1_p13 : 8'bz;  // Controlled_Buffer controlled_buffer_2
  assign cdm_8_mark5_1_p14 = rd_wr_prime ? IOdat : 8'bz;  // Controlled_Buffer controlled_buffer_3
  and and_3 (IOsel, and_4_out, proc, Data);
  // Probe on {cdm_8_mark5_1_p12, IOaddr}
  and and_4 (and_4_out, ~cdm_8_mark5_1_p12[1], ~cdm_8_mark5_1_p12[2], ~cdm_8_mark5_1_p12[3], cdm_8_mark5_1_p12[4], cdm_8_mark5_1_p12[5], cdm_8_mark5_1_p12[6], cdm_8_mark5_1_p12[7]);  // AND_Gate
  and and_5 (RAM, Data, ~IOsel);  // AND_Gate
  not not_2 (not_2_out, proc);
  // Probe on IOdat
  RAM ram_1 (
    .addr({cdm_8_mark5_1_p12, IOaddr}), .data(IOdat), .sel(RAM), .clk(not_2_out), .ld(rd_wr_prime));  // open: clr
  ROM rom_1 (.addr({cdm_8_mark5_1_p12, IOaddr}), .data(IOdat), .sel(Code));
  and and_6 (\new , IOsel, ~rd_wr_prime, ~IOaddr);  // AND_Gate
  Register register_1 (.D(IOdat), .Q(\output ), .clk(\new ));  // open: en, clr

  // Other names for the same wires on the sheet: output_t = \new 

  // Notes on the sheet:
  //   contents of rom_1 (hex, n*v repeats v):
  //   d2 1 d1 e0 a6 d1 e1 a6 d1 f1 a6 d2 7 d1 e2 a6 d2 d0 d3 e2 bf f e0 24 b8 0 e1 20 ee 33 ee 22 8e 8b ee
  //   15 d2 d0 d3 e2 bf f e0 33 d0 0 a8 8e 8b ee 29 d1 e1 b5 d0 e0 b0 61 8c d2 e0 a8 d0 e2 b0 44 e1 47 d0
  //   e2 b0 d1 e1 a4 d1 d0 11 89 b6 a e0 6d d3 d0 d2 7 a e0 6b bd 5 e1 67 d0 e2 b0 4c 8c 1d ee 6d ee 69 8f
  //   8a ee 56 ee 24 d2 1 d3 f1 ae bf f e0 6d d3 1 a7 d3 0 d1 f0 a4 d1 f1 a7 ee 10
endmodule

module field (
  input  move_left,
  input  pause,
  input  move_right,
  input  restart,
  input  rotate,
  output [7:0] next_1,
  output [9:0] row_1,
  output [7:0] next_2,
  output [9:0] row_2,
  output [7:0] next_3,
  output [9:0] row_3,
  output [7:0] next_4,
  output [7:0] next_5,
  output [9:0] row_4,
  output [7:0] next_6,
  output [9:0] row_5,
  output pause_out,
  output [9:0] row_6,
  output game_over,
  output [9:0] row_7,
  output [3:0] score_2,
  output [3:0] score_1,
  output [9:0] row_8,
  output [3:0] score0,
  output [3:0] score1,
  output [9:0] row_9,
  output [3:0] score2,
  output [3:0] score3,
  output [9:0] row_10,
  output [9:0] row_11,
  output [9:0] row_12,
  output [9:0] row_13,
  output [9:0] row_14,
  output [9:0] row_15,
  output [9:0] row_16,
  output [9:0] row_17,
  output [9:0] row_18,
  output [9:0] row_19,
  output [9:0] row_20
);

  wire and_1_out, and_2_out, and_3_out, and_4_out, and_5_out, and_6_out, and_7_out, and_8_out, and_9_out,
       and_11_out, bottom, buffer_1_out, buffer_4_out, buffer_5_out, buffer_6_out, clk,
       collision_1_collision_down, collision_1_collision_left, collision_1_collision_right,
       collision_1_collision_rotate, collision_down, collision_left, collision_right, collision_rotate,
       comparator_1_eq, comparator_2_eq, comparator_3_eq, comparator_4_eq, comparator_5_eq, d_ff_1_q,
       d_ff_3_q, d_ff_10_q, delete, deletion, game_clk, get, get_next, left_bord, left_bord_r, \new ,
       no_placement, not_3_out, not_4_out, not_5_out, not_6_out, not_7_out, not_8_out, not_9_out, not_10_out,
       not_11_out, not_12_out, not_13_out, not_14_out, not_15_out, not_16_out, not_17_out, not_18_out,
       not_19_out, not_20_out, not_21_out, not_22_out, not_23_out, not_24_out, not_25_out, not_26_out,
       not_27_out, not_28_out, not_29_out, not_31_out, not_32_out, not_33_out, not_34_out, not_35_out,
       not_36_out, or_5_out, or_6_out, or_7_out, or_8_out, or_9_out, or_11_out, or_12_out, or_14_out,
       or_15_out, or_16_out, or_18_out, proc_1_new, right_bord, right_bord_r, save, score_en, side_move,
       spawn;
  wire [1:0] counter;
  wire [2:0] num;
  wire [3:0] adder_1_out, l_x, multiplexer_1_out, multiplexer_2_out, r_x, subtractor_1_out, x;
  wire [7:0] bit_extender_9_out, collision_1_next_line, collision_2_next_line, collision_3_next_line,
       collision_4_next_line, collision_5_next_line, collision_6_next_line, collision_7_next_line,
       collision_8_next_line, collision_9_next_line, collision_10_next_line, collision_11_next_line,
       collision_12_next_line, collision_13_next_line, collision_14_next_line, collision_15_next_line,
       collision_16_next_line, collision_17_next_line, collision_18_next_line, collision_19_next_line,
       full_counter, proc_1_output, pull_resistor_5_node, pull_resistor_7_node, pull_resistor_8_node,
       register_4_q, register_5_q, sprite_mover_1_full_count_out, sprite_mover_1_next_line,
       sprite_mover_2_full_count_out, sprite_mover_2_next_line, sprite_mover_3_full_count_out,
       sprite_mover_3_next_line, sprite_mover_4_full_count_out, sprite_mover_4_next_line,
       sprite_mover_5_full_count_out, sprite_mover_5_next_line, sprite_mover_6_full_count_out,
       sprite_mover_6_next_line, sprite_mover_7_full_count_out, sprite_mover_7_next_line,
       sprite_mover_8_full_count_out, sprite_mover_8_next_line, sprite_mover_9_full_count_out,
       sprite_mover_9_next_line, sprite_mover_10_full_count_out, sprite_mover_10_next_line,
       sprite_mover_11_full_count_out, sprite_mover_11_next_line, sprite_mover_12_full_count_out,
       sprite_mover_12_next_line, sprite_mover_13_full_count_out, sprite_mover_13_next_line,
       sprite_mover_14_full_count_out, sprite_mover_14_next_line, sprite_mover_15_full_count_out,
       sprite_mover_15_next_line, sprite_mover_16_full_count_out, sprite_mover_16_next_line,
       sprite_mover_17_full_count_out, sprite_mover_17_next_line, sprite_mover_18_full_count_out,
       sprite_mover_18_next_line, sprite_mover_19_full_count_out, sprite_mover_19_next_line,
       sprite_mover_20_full_count_out, sprite_mover_20_next_line, sprite_mover_21_full_count_out,
       sprite_mover_21_next_line, sprite_mover_22_full_count_out, sprite_mover_22_next_line,
       sprite_mover_23_full_count_out, sprite_mover_23_next_line, sprite_mover_24_full_count_out,
       sprite_mover_24_next_line, sprite_mover_25_full_count_out, sprite_mover_25_next_line,
       sprite_mover_26_full_count_out, sprite_mover_26_next_line, subtractor_2_out, y;
  wire [9:0] f1, f2, f3, f4, fr1, fr2, fr3, fr4, l1_b, l20_b, l_1, l_2, l_3, l_4, or_10_out,
       pull_resistor_6_node, sprite_mover_1_out, sprite_mover_2_out, sprite_mover_3_out, sprite_mover_4_out,
       sprite_mover_5_out, sprite_mover_6_background_out, sprite_mover_6_out, sprite_mover_7_background_out,
       sprite_mover_7_out, sprite_mover_8_background_out, sprite_mover_8_out, sprite_mover_9_background_out,
       sprite_mover_9_out, sprite_mover_10_background_out, sprite_mover_10_out,
       sprite_mover_11_background_out, sprite_mover_11_out, sprite_mover_12_background_out,
       sprite_mover_12_out, sprite_mover_13_background_out, sprite_mover_13_out,
       sprite_mover_14_background_out, sprite_mover_14_out, sprite_mover_15_background_out,
       sprite_mover_15_out, sprite_mover_16_background_out, sprite_mover_16_out,
       sprite_mover_17_background_out, sprite_mover_17_out, sprite_mover_18_background_out,
       sprite_mover_18_out, sprite_mover_19_background_out, sprite_mover_19_out,
       sprite_mover_20_background_out, sprite_mover_20_out, sprite_mover_21_background_out,
       sprite_mover_21_out, sprite_mover_22_background_out, sprite_mover_22_out,
       sprite_mover_23_background_out, sprite_mover_23_out, sprite_mover_24_out, sprite_mover_25_out,
       sprite_mover_26_out, xor_1_out;
  wire [15:0] bit_extender_1_out, bit_extender_2_out, bit_extender_3_out, bit_extender_4_out,
       bit_extender_11_out, bit_extender_12_out, bit_extender_13_out, bit_extender_14_out, curr_figure,
       curr_rotated, multiplexer_3_out, multiplexer_4_out, next_figure, or_17_out, score_temp, shifter_1_out,
       shifter_2_out, shifter_3_out, shifter_4_out, shifter_5_out, shifter_6_out, shifter_7_out,
       shifter_8_out, shifter_9_out, shifter_10_out, shifter_11_out, shifter_12_out, shifter_13_out,
       shifter_14_out, shifter_15_out, shifter_16_out, shifter_17_out, shifter_18_out;

  or or_1 (collision_rotate, left_bord_r, right_bord_r, collision_1_collision_rotate);
  or or_2 (collision_left, left_bord, collision_1_collision_left);
  or or_3 (collision_down, bottom, collision_1_collision_down);
  or or_4 (collision_right, right_bord, collision_1_collision_right);
  collision collision_1 (
    .line_in(pull_resistor_5_node), .y_placement(y), .sprite_top(f1), .sprite_topmid(f2), .sprite_botmid(f3),
    .sprite_bottom(f4), .background_row(l1_b), .next_line(collision_1_next_line),
    .collision_left(collision_1_collision_left), .collision_right(collision_1_collision_right),
    .collision_down(collision_1_collision_down), .r_sprite_top(fr1), .r_sprite_topmid(fr2),
    .r_sprite_botmid(fr3), .r_sprite_bot(fr4), .collision_rotate(collision_1_collision_rotate));
  collision collision_2 (
    .line_in(collision_1_next_line), .y_placement(y), .sprite_top(f1), .sprite_topmid(f2),
    .sprite_botmid(f3), .sprite_bottom(f4), .background_row(sprite_mover_6_background_out),
    .next_line(collision_2_next_line), .collision_left(collision_1_collision_left),
    .collision_right(collision_1_collision_right), .collision_down(collision_1_collision_down),
    .r_sprite_top(fr1), .r_sprite_topmid(fr2), .r_sprite_botmid(fr3), .r_sprite_bot(fr4),
    .collision_rotate(collision_1_collision_rotate));
  collision collision_3 (
    .line_in(collision_2_next_line), .y_placement(y), .sprite_top(f1), .sprite_topmid(f2),
    .sprite_botmid(f3), .sprite_bottom(f4), .background_row(sprite_mover_7_background_out),
    .next_line(collision_3_next_line), .collision_left(collision_1_collision_left),
    .collision_right(collision_1_collision_right), .collision_down(collision_1_collision_down),
    .r_sprite_top(fr1), .r_sprite_topmid(fr2), .r_sprite_botmid(fr3), .r_sprite_bot(fr4),
    .collision_rotate(collision_1_collision_rotate));
  collision collision_4 (
    .line_in(collision_3_next_line), .y_placement(y), .sprite_top(f1), .sprite_topmid(f2),
    .sprite_botmid(f3), .sprite_bottom(f4), .background_row(sprite_mover_8_background_out),
    .next_line(collision_4_next_line), .collision_left(collision_1_collision_left),
    .collision_right(collision_1_collision_right), .collision_down(collision_1_collision_down),
    .r_sprite_top(fr1), .r_sprite_topmid(fr2), .r_sprite_botmid(fr3), .r_sprite_bot(fr4),
    .collision_rotate(collision_1_collision_rotate));
  collision collision_5 (
    .line_in(collision_4_next_line), .y_placement(y), .sprite_top(f1), .sprite_topmid(f2),
    .sprite_botmid(f3), .sprite_bottom(f4), .background_row(sprite_mover_9_background_out),
    .next_line(collision_5_next_line), .collision_left(collision_1_collision_left),
    .collision_right(collision_1_collision_right), .collision_down(collision_1_collision_down),
    .r_sprite_top(fr1), .r_sprite_topmid(fr2), .r_sprite_botmid(fr3), .r_sprite_bot(fr4),
    .collision_rotate(collision_1_collision_rotate));
  collision collision_6 (
    .line_in(collision_5_next_line), .y_placement(y), .sprite_top(f1), .sprite_topmid(f2),
    .sprite_botmid(f3), .sprite_bottom(f4), .background_row(sprite_mover_10_background_out),
    .next_line(collision_6_next_line), .collision_left(collision_1_collision_left),
    .collision_right(collision_1_collision_right), .collision_down(collision_1_collision_down),
    .r_sprite_top(fr1), .r_sprite_topmid(fr2), .r_sprite_botmid(fr3), .r_sprite_bot(fr4),
    .collision_rotate(collision_1_collision_rotate));
  collision collision_7 (
    .line_in(collision_6_next_line), .y_placement(y), .sprite_top(f1), .sprite_topmid(f2),
    .sprite_botmid(f3), .sprite_bottom(f4), .background_row(sprite_mover_11_background_out),
    .next_line(collision_7_next_line), .collision_left(collision_1_collision_left),
    .collision_right(collision_1_collision_right), .collision_down(collision_1_collision_down),
    .r_sprite_top(fr1), .r_sprite_topmid(fr2), .r_sprite_botmid(fr3), .r_sprite_bot(fr4),
    .collision_rotate(collision_1_collision_rotate));
  collision collision_8 (
    .line_in(collision_7_next_line), .y_placement(y), .sprite_top(f1), .sprite_topmid(f2),
    .sprite_botmid(f3), .sprite_bottom(f4), .background_row(sprite_mover_12_background_out),
    .next_line(collision_8_next_line), .collision_left(collision_1_collision_left),
    .collision_right(collision_1_collision_right), .collision_down(collision_1_collision_down),
    .r_sprite_top(fr1), .r_sprite_topmid(fr2), .r_sprite_botmid(fr3), .r_sprite_bot(fr4),
    .collision_rotate(collision_1_collision_rotate));
  collision collision_9 (
    .line_in(collision_8_next_line), .y_placement(y), .sprite_top(f1), .sprite_topmid(f2),
    .sprite_botmid(f3), .sprite_bottom(f4), .background_row(sprite_mover_13_background_out),
    .next_line(collision_9_next_line), .collision_left(collision_1_collision_left),
    .collision_right(collision_1_collision_right), .collision_down(collision_1_collision_down),
    .r_sprite_top(fr1), .r_sprite_topmid(fr2), .r_sprite_botmid(fr3), .r_sprite_bot(fr4),
    .collision_rotate(collision_1_collision_rotate));
  collision collision_10 (
    .line_in(collision_9_next_line), .y_placement(y), .sprite_top(f1), .sprite_topmid(f2),
    .sprite_botmid(f3), .sprite_bottom(f4), .background_row(sprite_mover_14_background_out),
    .next_line(collision_10_next_line), .collision_left(collision_1_collision_left),
    .collision_right(collision_1_collision_right), .collision_down(collision_1_collision_down),
    .r_sprite_top(fr1), .r_sprite_topmid(fr2), .r_sprite_botmid(fr3), .r_sprite_bot(fr4),
    .collision_rotate(collision_1_collision_rotate));
  collision collision_11 (
    .line_in(collision_10_next_line), .y_placement(y), .sprite_top(f1), .sprite_topmid(f2),
    .sprite_botmid(f3), .sprite_bottom(f4), .background_row(sprite_mover_15_background_out),
    .next_line(collision_11_next_line), .collision_left(collision_1_collision_left),
    .collision_right(collision_1_collision_right), .collision_down(collision_1_collision_down),
    .r_sprite_top(fr1), .r_sprite_topmid(fr2), .r_sprite_botmid(fr3), .r_sprite_bot(fr4),
    .collision_rotate(collision_1_collision_rotate));
  collision collision_12 (
    .line_in(collision_11_next_line), .y_placement(y), .sprite_top(f1), .sprite_topmid(f2),
    .sprite_botmid(f3), .sprite_bottom(f4), .background_row(sprite_mover_16_background_out),
    .next_line(collision_12_next_line), .collision_left(collision_1_collision_left),
    .collision_right(collision_1_collision_right), .collision_down(collision_1_collision_down),
    .r_sprite_top(fr1), .r_sprite_topmid(fr2), .r_sprite_botmid(fr3), .r_sprite_bot(fr4),
    .collision_rotate(collision_1_collision_rotate));
  collision collision_13 (
    .line_in(collision_12_next_line), .y_placement(y), .sprite_top(f1), .sprite_topmid(f2),
    .sprite_botmid(f3), .sprite_bottom(f4), .background_row(sprite_mover_17_background_out),
    .next_line(collision_13_next_line), .collision_left(collision_1_collision_left),
    .collision_right(collision_1_collision_right), .collision_down(collision_1_collision_down),
    .r_sprite_top(fr1), .r_sprite_topmid(fr2), .r_sprite_botmid(fr3), .r_sprite_bot(fr4),
    .collision_rotate(collision_1_collision_rotate));
  collision collision_14 (
    .line_in(collision_13_next_line), .y_placement(y), .sprite_top(f1), .sprite_topmid(f2),
    .sprite_botmid(f3), .sprite_bottom(f4), .background_row(sprite_mover_18_background_out),
    .next_line(collision_14_next_line), .collision_left(collision_1_collision_left),
    .collision_right(collision_1_collision_right), .collision_down(collision_1_collision_down),
    .r_sprite_top(fr1), .r_sprite_topmid(fr2), .r_sprite_botmid(fr3), .r_sprite_bot(fr4),
    .collision_rotate(collision_1_collision_rotate));
  collision collision_15 (
    .line_in(collision_14_next_line), .y_placement(y), .sprite_top(f1), .sprite_topmid(f2),
    .sprite_botmid(f3), .sprite_bottom(f4), .background_row(sprite_mover_19_background_out),
    .next_line(collision_15_next_line), .collision_left(collision_1_collision_left),
    .collision_right(collision_1_collision_right), .collision_down(collision_1_collision_down),
    .r_sprite_top(fr1), .r_sprite_topmid(fr2), .r_sprite_botmid(fr3), .r_sprite_bot(fr4),
    .collision_rotate(collision_1_collision_rotate));
  collision collision_16 (
    .line_in(collision_15_next_line), .y_placement(y), .sprite_top(f1), .sprite_topmid(f2),
    .sprite_botmid(f3), .sprite_bottom(f4), .background_row(sprite_mover_20_background_out),
    .next_line(collision_16_next_line), .collision_left(collision_1_collision_left),
    .collision_right(collision_1_collision_right), .collision_down(collision_1_collision_down),
    .r_sprite_top(fr1), .r_sprite_topmid(fr2), .r_sprite_botmid(fr3), .r_sprite_bot(fr4),
    .collision_rotate(collision_1_collision_rotate));
  collision collision_17 (
    .line_in(collision_16_next_line), .y_placement(y), .sprite_top(f1), .sprite_topmid(f2),
    .sprite_botmid(f3), .sprite_bottom(f4), .background_row(sprite_mover_21_background_out),
    .next_line(collision_17_next_line), .collision_left(collision_1_collision_left),
    .collision_right(collision_1_collision_right), .collision_down(collision_1_collision_down),
    .r_sprite_top(fr1), .r_sprite_topmid(fr2), .r_sprite_botmid(fr3), .r_sprite_bot(fr4),
    .collision_rotate(collision_1_collision_rotate));
  collision collision_18 (
    .line_in(collision_17_next_line), .y_placement(y), .sprite_top(f1), .sprite_topmid(f2),
    .sprite_botmid(f3), .sprite_bottom(f4), .background_row(sprite_mover_22_background_out),
    .next_line(collision_18_next_line), .collision_left(collision_1_collision_left),
    .collision_right(collision_1_collision_right), .collision_down(collision_1_collision_down),
    .r_sprite_top(fr1), .r_sprite_topmid(fr2), .r_sprite_botmid(fr3), .r_sprite_bot(fr4),
    .collision_rotate(collision_1_collision_rotate));
  collision collision_19 (
    .line_in(collision_18_next_line), .y_placement(y), .sprite_top(f1), .sprite_topmid(f2),
    .sprite_botmid(f3), .sprite_bottom(f4), .background_row(sprite_mover_23_background_out),
    .next_line(collision_19_next_line), .collision_left(collision_1_collision_left),
    .collision_right(collision_1_collision_right), .collision_down(collision_1_collision_down),
    .r_sprite_top(fr1), .r_sprite_topmid(fr2), .r_sprite_botmid(fr3), .r_sprite_bot(fr4),
    .collision_rotate(collision_1_collision_rotate));
  collision collision_20 (
    .line_in(collision_19_next_line), .y_placement(y), .sprite_top(f1), .sprite_topmid(f2),
    .sprite_botmid(f3), .sprite_bottom(f4), .background_row(l20_b),
    .collision_left(collision_1_collision_left), .collision_right(collision_1_collision_right),
    .collision_down(collision_1_collision_down), .r_sprite_top(fr1), .r_sprite_topmid(fr2),
    .r_sprite_botmid(fr3), .r_sprite_bot(fr4), .collision_rotate(collision_1_collision_rotate));  // open: next_line
  Pull_Resistor pull_resistor_1 (.node(collision_1_collision_down));
  Pull_Resistor pull_resistor_2 (.node(collision_1_collision_left));
  Pull_Resistor pull_resistor_3 (.node(collision_1_collision_rotate));
  Pull_Resistor pull_resistor_4 (.node(collision_1_collision_right));
  Pull_Resistor pull_resistor_5 (.node(pull_resistor_5_node));
  // Probe on l1_b
  // Probe on sprite_mover_6_background_out
  // Probe on sprite_mover_7_background_out
  // Probe on sprite_mover_8_background_out
  // Probe on sprite_mover_9_background_out
  // Probe on sprite_mover_10_background_out
  // Probe on sprite_mover_11_background_out
  // Probe on sprite_mover_12_background_out
  // Probe on sprite_mover_13_background_out
  // Probe on sprite_mover_14_background_out
  // Probe on sprite_mover_15_background_out
  // Probe on sprite_mover_16_background_out
  // Probe on sprite_mover_17_background_out
  // Probe on sprite_mover_18_background_out
  // Probe on sprite_mover_19_background_out
  // Probe on sprite_mover_20_background_out
  // Probe on sprite_mover_21_background_out
  // Probe on sprite_mover_22_background_out
  // Probe on sprite_mover_23_background_out
  // Probe on l20_b
  Pull_Resistor pull_resistor_6 (.node(pull_resistor_6_node));
  Pull_Resistor pull_resistor_7 (.node(pull_resistor_7_node));
  sprite_mover sprite_mover_1 (
    .line_in(pull_resistor_8_node), .next_line(sprite_mover_1_next_line), .sprite_top(f1),
    .sprite_topmid(f2), .sprite_botmid(f3), .sprite_bottom(f4), .y_placement(y), .out(sprite_mover_1_out),
    .save_to_background(save), .delete_row(delete), .full_row_in(pull_resistor_6_node), .row_out(l_4),
    .full_count_in(pull_resistor_7_node), .full_count_out(sprite_mover_1_full_count_out), .erase(get_next),
    .sprite_top_2(fr1), .sprite_topmid_2(fr2), .sprite_botmid_2(fr3), .sprite_bottom_2(fr4));  // open: background_out
  sprite_mover sprite_mover_2 (
    .line_in(sprite_mover_1_next_line), .next_line(sprite_mover_2_next_line), .sprite_top(f1),
    .sprite_topmid(f2), .sprite_botmid(f3), .sprite_bottom(f4), .y_placement(y), .out(sprite_mover_2_out),
    .save_to_background(save), .delete_row(delete), .full_row_in(sprite_mover_1_out), .row_out(l_3),
    .full_count_in(sprite_mover_1_full_count_out), .full_count_out(sprite_mover_2_full_count_out),
    .erase(get_next), .sprite_top_2(fr1), .sprite_topmid_2(fr2), .sprite_botmid_2(fr3), .sprite_bottom_2(fr4));  // open: background_out
  sprite_mover sprite_mover_3 (
    .line_in(sprite_mover_2_next_line), .next_line(sprite_mover_3_next_line), .sprite_top(f1),
    .sprite_topmid(f2), .sprite_botmid(f3), .sprite_bottom(f4), .y_placement(y), .out(sprite_mover_3_out),
    .save_to_background(save), .delete_row(delete), .full_row_in(sprite_mover_2_out), .row_out(l_2),
    .full_count_in(sprite_mover_2_full_count_out), .full_count_out(sprite_mover_3_full_count_out),
    .erase(get_next), .sprite_top_2(fr1), .sprite_topmid_2(fr2), .sprite_botmid_2(fr3), .sprite_bottom_2(fr4));  // open: background_out
  sprite_mover sprite_mover_4 (
    .line_in(sprite_mover_3_next_line), .next_line(sprite_mover_4_next_line), .sprite_top(f1),
    .sprite_topmid(f2), .sprite_botmid(f3), .sprite_bottom(f4), .y_placement(y), .out(sprite_mover_4_out),
    .save_to_background(save), .delete_row(delete), .full_row_in(sprite_mover_3_out), .row_out(l_1),
    .full_count_in(sprite_mover_3_full_count_out), .full_count_out(sprite_mover_4_full_count_out),
    .erase(get_next), .sprite_top_2(fr1), .sprite_topmid_2(fr2), .sprite_botmid_2(fr3), .sprite_bottom_2(fr4));  // open: background_out
  sprite_mover sprite_mover_5 (
    .line_in(sprite_mover_4_next_line), .next_line(sprite_mover_5_next_line), .sprite_top(f1),
    .sprite_topmid(f2), .sprite_botmid(f3), .sprite_bottom(f4), .y_placement(y), .background_out(l1_b),
    .out(sprite_mover_5_out), .save_to_background(save), .delete_row(delete),
    .full_row_in(sprite_mover_4_out), .row_out(row_1), .full_count_in(sprite_mover_4_full_count_out),
    .full_count_out(sprite_mover_5_full_count_out), .erase(restart), .sprite_top_2(fr1),
    .sprite_topmid_2(fr2), .sprite_botmid_2(fr3), .sprite_bottom_2(fr4));
  sprite_mover sprite_mover_6 (
    .line_in(sprite_mover_5_next_line), .next_line(sprite_mover_6_next_line), .sprite_top(f1),
    .sprite_topmid(f2), .sprite_botmid(f3), .sprite_bottom(f4), .y_placement(y),
    .background_out(sprite_mover_6_background_out), .out(sprite_mover_6_out), .save_to_background(save),
    .delete_row(delete), .full_row_in(sprite_mover_5_out), .row_out(row_2),
    .full_count_in(sprite_mover_5_full_count_out), .full_count_out(sprite_mover_6_full_count_out),
    .erase(restart), .sprite_top_2(fr1), .sprite_topmid_2(fr2), .sprite_botmid_2(fr3), .sprite_bottom_2(fr4));
  sprite_mover sprite_mover_7 (
    .line_in(sprite_mover_6_next_line), .next_line(sprite_mover_7_next_line), .sprite_top(f1),
    .sprite_topmid(f2), .sprite_botmid(f3), .sprite_bottom(f4), .y_placement(y),
    .background_out(sprite_mover_7_background_out), .out(sprite_mover_7_out), .save_to_background(save),
    .delete_row(delete), .full_row_in(sprite_mover_6_out), .row_out(row_3),
    .full_count_in(sprite_mover_6_full_count_out), .full_count_out(sprite_mover_7_full_count_out),
    .erase(restart), .sprite_top_2(fr1), .sprite_topmid_2(fr2), .sprite_botmid_2(fr3), .sprite_bottom_2(fr4));
  sprite_mover sprite_mover_8 (
    .line_in(sprite_mover_7_next_line), .next_line(sprite_mover_8_next_line), .sprite_top(f1),
    .sprite_topmid(f2), .sprite_botmid(f3), .sprite_bottom(f4), .y_placement(y),
    .background_out(sprite_mover_8_background_out), .out(sprite_mover_8_out), .save_to_background(save),
    .delete_row(delete), .full_row_in(sprite_mover_7_out), .row_out(row_4),
    .full_count_in(sprite_mover_7_full_count_out), .full_count_out(sprite_mover_8_full_count_out),
    .erase(restart), .sprite_top_2(fr1), .sprite_topmid_2(fr2), .sprite_botmid_2(fr3), .sprite_bottom_2(fr4));
  sprite_mover sprite_mover_9 (
    .line_in(sprite_mover_8_next_line), .next_line(sprite_mover_9_next_line), .sprite_top(f1),
    .sprite_topmid(f2), .sprite_botmid(f3), .sprite_bottom(f4), .y_placement(y),
    .background_out(sprite_mover_9_background_out), .out(sprite_mover_9_out), .save_to_background(save),
    .delete_row(delete), .full_row_in(sprite_mover_8_out), .row_out(row_5),
    .full_count_in(sprite_mover_8_full_count_out), .full_count_out(sprite_mover_9_full_count_out),
    .erase(restart), .sprite_top_2(fr1), .sprite_topmid_2(fr2), .sprite_botmid_2(fr3), .sprite_bottom_2(fr4));
  sprite_mover sprite_mover_10 (
    .line_in(sprite_mover_9_next_line), .next_line(sprite_mover_10_next_line), .sprite_top(f1),
    .sprite_topmid(f2), .sprite_botmid(f3), .sprite_bottom(f4), .y_placement(y),
    .background_out(sprite_mover_10_background_out), .out(sprite_mover_10_out), .save_to_background(save),
    .delete_row(delete), .full_row_in(sprite_mover_9_out), .row_out(row_6),
    .full_count_in(sprite_mover_9_full_count_out), .full_count_out(sprite_mover_10_full_count_out),
    .erase(restart), .sprite_top_2(fr1), .sprite_topmid_2(fr2), .sprite_botmid_2(fr3), .sprite_bottom_2(fr4));
  sprite_mover sprite_mover_11 (
    .line_in(sprite_mover_10_next_line), .next_line(sprite_mover_11_next_line), .sprite_top(f1),
    .sprite_topmid(f2), .sprite_botmid(f3), .sprite_bottom(f4), .y_placement(y),
    .background_out(sprite_mover_11_background_out), .out(sprite_mover_11_out), .save_to_background(save),
    .delete_row(delete), .full_row_in(sprite_mover_10_out), .row_out(row_7),
    .full_count_in(sprite_mover_10_full_count_out), .full_count_out(sprite_mover_11_full_count_out),
    .erase(restart), .sprite_top_2(fr1), .sprite_topmid_2(fr2), .sprite_botmid_2(fr3), .sprite_bottom_2(fr4));
  sprite_mover sprite_mover_12 (
    .line_in(sprite_mover_11_next_line), .next_line(sprite_mover_12_next_line), .sprite_top(f1),
    .sprite_topmid(f2), .sprite_botmid(f3), .sprite_bottom(f4), .y_placement(y),
    .background_out(sprite_mover_12_background_out), .out(sprite_mover_12_out), .save_to_background(save),
    .delete_row(delete), .full_row_in(sprite_mover_11_out), .row_out(row_8),
    .full_count_in(sprite_mover_11_full_count_out), .full_count_out(sprite_mover_12_full_count_out),
    .erase(restart), .sprite_top_2(fr1), .sprite_topmid_2(fr2), .sprite_botmid_2(fr3), .sprite_bottom_2(fr4));
  sprite_mover sprite_mover_13 (
    .line_in(sprite_mover_12_next_line), .next_line(sprite_mover_13_next_line), .sprite_top(f1),
    .sprite_topmid(f2), .sprite_botmid(f3), .sprite_bottom(f4), .y_placement(y),
    .background_out(sprite_mover_13_background_out), .out(sprite_mover_13_out), .save_to_background(save),
    .delete_row(delete), .full_row_in(sprite_mover_12_out), .row_out(row_9),
    .full_count_in(sprite_mover_12_full_count_out), .full_count_out(sprite_mover_13_full_count_out),
    .erase(restart), .sprite_top_2(fr1), .sprite_topmid_2(fr2), .sprite_botmid_2(fr3), .sprite_bottom_2(fr4));
  sprite_mover sprite_mover_14 (
    .line_in(sprite_mover_13_next_line), .next_line(sprite_mover_14_next_line), .sprite_top(f1),
    .sprite_topmid(f2), .sprite_botmid(f3), .sprite_bottom(f4), .y_placement(y),
    .background_out(sprite_mover_14_background_out), .out(sprite_mover_14_out), .save_to_background(save),
    .delete_row(delete), .full_row_in(sprite_mover_13_out), .row_out(row_10),
    .full_count_in(sprite_mover_13_full_count_out), .full_count_out(sprite_mover_14_full_count_out),
    .erase(restart), .sprite_top_2(fr1), .sprite_topmid_2(fr2), .sprite_botmid_2(fr3), .sprite_bottom_2(fr4));
  sprite_mover sprite_mover_15 (
    .line_in(sprite_mover_14_next_line), .next_line(sprite_mover_15_next_line), .sprite_top(f1),
    .sprite_topmid(f2), .sprite_botmid(f3), .sprite_bottom(f4), .y_placement(y),
    .background_out(sprite_mover_15_background_out), .out(sprite_mover_15_out), .save_to_background(save),
    .delete_row(delete), .full_row_in(sprite_mover_14_out), .row_out(row_11),
    .full_count_in(sprite_mover_14_full_count_out), .full_count_out(sprite_mover_15_full_count_out),
    .erase(restart), .sprite_top_2(fr1), .sprite_topmid_2(fr2), .sprite_botmid_2(fr3), .sprite_bottom_2(fr4));
  sprite_mover sprite_mover_16 (
    .line_in(sprite_mover_15_next_line), .next_line(sprite_mover_16_next_line), .sprite_top(f1),
    .sprite_topmid(f2), .sprite_botmid(f3), .sprite_bottom(f4), .y_placement(y),
    .background_out(sprite_mover_16_background_out), .out(sprite_mover_16_out), .save_to_background(save),
    .delete_row(delete), .full_row_in(sprite_mover_15_out), .row_out(row_12),
    .full_count_in(sprite_mover_15_full_count_out), .full_count_out(sprite_mover_16_full_count_out),
    .erase(restart), .sprite_top_2(fr1), .sprite_topmid_2(fr2), .sprite_botmid_2(fr3), .sprite_bottom_2(fr4));
  sprite_mover sprite_mover_17 (
    .line_in(sprite_mover_16_next_line), .next_line(sprite_mover_17_next_line), .sprite_top(f1),
    .sprite_topmid(f2), .sprite_botmid(f3), .sprite_bottom(f4), .y_placement(y),
    .background_out(sprite_mover_17_background_out), .out(sprite_mover_17_out), .save_to_background(save),
    .delete_row(delete), .full_row_in(sprite_mover_16_out), .row_out(row_13),
    .full_count_in(sprite_mover_16_full_count_out), .full_count_out(sprite_mover_17_full_count_out),
    .erase(restart), .sprite_top_2(fr1), .sprite_topmid_2(fr2), .sprite_botmid_2(fr3), .sprite_bottom_2(fr4));
  sprite_mover sprite_mover_18 (
    .line_in(sprite_mover_17_next_line), .next_line(sprite_mover_18_next_line), .sprite_top(f1),
    .sprite_topmid(f2), .sprite_botmid(f3), .sprite_bottom(f4), .y_placement(y),
    .background_out(sprite_mover_18_background_out), .out(sprite_mover_18_out), .save_to_background(save),
    .delete_row(delete), .full_row_in(sprite_mover_17_out), .row_out(row_14),
    .full_count_in(sprite_mover_17_full_count_out), .full_count_out(sprite_mover_18_full_count_out),
    .erase(restart), .sprite_top_2(fr1), .sprite_topmid_2(fr2), .sprite_botmid_2(fr3), .sprite_bottom_2(fr4));
  sprite_mover sprite_mover_19 (
    .line_in(sprite_mover_18_next_line), .next_line(sprite_mover_19_next_line), .sprite_top(f1),
    .sprite_topmid(f2), .sprite_botmid(f3), .sprite_bottom(f4), .y_placement(y),
    .background_out(sprite_mover_19_background_out), .out(sprite_mover_19_out), .save_to_background(save),
    .delete_row(delete), .full_row_in(sprite_mover_18_out), .row_out(row_15),
    .full_count_in(sprite_mover_18_full_count_out), .full_count_out(sprite_mover_19_full_count_out),
    .erase(restart), .sprite_top_2(fr1), .sprite_topmid_2(fr2), .sprite_botmid_2(fr3), .sprite_bottom_2(fr4));
  sprite_mover sprite_mover_20 (
    .line_in(sprite_mover_19_next_line), .next_line(sprite_mover_20_next_line), .sprite_top(f1),
    .sprite_topmid(f2), .sprite_botmid(f3), .sprite_bottom(f4), .y_placement(y),
    .background_out(sprite_mover_20_background_out), .out(sprite_mover_20_out), .save_to_background(save),
    .delete_row(delete), .full_row_in(sprite_mover_19_out), .row_out(row_16),
    .full_count_in(sprite_mover_19_full_count_out), .full_count_out(sprite_mover_20_full_count_out),
    .erase(restart), .sprite_top_2(fr1), .sprite_topmid_2(fr2), .sprite_botmid_2(fr3), .sprite_bottom_2(fr4));
  sprite_mover sprite_mover_21 (
    .line_in(sprite_mover_20_next_line), .next_line(sprite_mover_21_next_line), .sprite_top(f1),
    .sprite_topmid(f2), .sprite_botmid(f3), .sprite_bottom(f4), .y_placement(y),
    .background_out(sprite_mover_21_background_out), .out(sprite_mover_21_out), .save_to_background(save),
    .delete_row(delete), .full_row_in(sprite_mover_20_out), .row_out(row_17),
    .full_count_in(sprite_mover_20_full_count_out), .full_count_out(sprite_mover_21_full_count_out),
    .erase(restart), .sprite_top_2(fr1), .sprite_topmid_2(fr2), .sprite_botmid_2(fr3), .sprite_bottom_2(fr4));
  sprite_mover sprite_mover_22 (
    .line_in(sprite_mover_21_next_line), .next_line(sprite_mover_22_next_line), .sprite_top(f1),
    .sprite_topmid(f2), .sprite_botmid(f3), .sprite_bottom(f4), .y_placement(y),
    .background_out(sprite_mover_22_background_out), .out(sprite_mover_22_out), .save_to_background(save),
    .delete_row(delete), .full_row_in(sprite_mover_21_out), .row_out(row_18),
    .full_count_in(sprite_mover_21_full_count_out), .full_count_out(sprite_mover_22_full_count_out),
    .erase(restart), .sprite_top_2(fr1), .sprite_topmid_2(fr2), .sprite_botmid_2(fr3), .sprite_bottom_2(fr4));
  sprite_mover sprite_mover_23 (
    .line_in(sprite_mover_22_next_line), .next_line(sprite_mover_23_next_line), .sprite_top(f1),
    .sprite_topmid(f2), .sprite_botmid(f3), .sprite_bottom(f4), .y_placement(y),
    .background_out(sprite_mover_23_background_out), .out(sprite_mover_23_out), .save_to_background(save),
    .delete_row(delete), .full_row_in(sprite_mover_22_out), .row_out(row_19),
    .full_count_in(sprite_mover_22_full_count_out), .full_count_out(sprite_mover_23_full_count_out),
    .erase(restart), .sprite_top_2(fr1), .sprite_topmid_2(fr2), .sprite_botmid_2(fr3), .sprite_bottom_2(fr4));
  sprite_mover sprite_mover_24 (
    .line_in(sprite_mover_23_next_line), .next_line(sprite_mover_24_next_line), .sprite_top(f1),
    .sprite_topmid(f2), .sprite_botmid(f3), .sprite_bottom(f4), .y_placement(y), .background_out(l20_b),
    .out(sprite_mover_24_out), .save_to_background(save), .delete_row(delete),
    .full_row_in(sprite_mover_23_out), .row_out(row_20), .full_count_in(sprite_mover_23_full_count_out),
    .full_count_out(sprite_mover_24_full_count_out), .erase(restart), .sprite_top_2(fr1),
    .sprite_topmid_2(fr2), .sprite_botmid_2(fr3), .sprite_bottom_2(fr4));
  sprite_mover sprite_mover_25 (
    .line_in(sprite_mover_24_next_line), .next_line(sprite_mover_25_next_line), .sprite_top(f1),
    .sprite_topmid(f2), .sprite_botmid(f3), .sprite_bottom(f4), .y_placement(y), .out(sprite_mover_25_out),
    .save_to_background(save), .delete_row(delete), .full_row_in(sprite_mover_24_out),
    .full_count_in(sprite_mover_24_full_count_out), .full_count_out(sprite_mover_25_full_count_out),
    .erase(restart), .sprite_top_2(fr1), .sprite_topmid_2(fr2), .sprite_botmid_2(fr3), .sprite_bottom_2(fr4));  // open: background_out, row_out
  sprite_mover sprite_mover_26 (
    .line_in(sprite_mover_25_next_line), .next_line(sprite_mover_26_next_line), .sprite_top(f1),
    .sprite_topmid(f2), .sprite_botmid(f3), .sprite_bottom(f4), .y_placement(y), .out(sprite_mover_26_out),
    .save_to_background(save), .delete_row(delete), .full_row_in(sprite_mover_25_out),
    .full_count_in(sprite_mover_25_full_count_out), .full_count_out(sprite_mover_26_full_count_out),
    .erase(restart), .sprite_top_2(fr1), .sprite_topmid_2(fr2), .sprite_botmid_2(fr3), .sprite_bottom_2(fr4));  // open: background_out, row_out
  sprite_mover sprite_mover_27 (
    .line_in(sprite_mover_26_next_line), .sprite_top(f1), .sprite_topmid(f2), .sprite_botmid(f3),
    .sprite_bottom(f4), .y_placement(y), .save_to_background(save), .delete_row(delete),
    .full_row_in(sprite_mover_26_out), .full_count_in(sprite_mover_26_full_count_out),
    .full_count_out(full_counter), .erase(restart), .sprite_top_2(fr1), .sprite_topmid_2(fr2),
    .sprite_botmid_2(fr3), .sprite_bottom_2(fr4));  // open: next_line, background_out, out, row_out
  Pull_Resistor pull_resistor_8 (.node(pull_resistor_8_node));
  Comparator #(.width(10)) comparator_1 (.a(l1_b), .b({10{1'b0}}), .eq(comparator_1_eq));  // open: gt, lt
  and and_1 (and_1_out, collision_down, ~pause_out);  // AND_Gate
  assign bit_extender_1_out = {{12{1'b0}}, curr_figure[3:0]};  // Bit_Extender bit_extender_1
  assign bit_extender_2_out = {{12{1'b0}}, curr_figure[7:4]};  // Bit_Extender bit_extender_2
  assign bit_extender_3_out = {{12{1'b0}}, curr_figure[11:8]};  // Bit_Extender bit_extender_3
  assign bit_extender_4_out = {{12{1'b0}}, curr_figure[15:12]};  // Bit_Extender bit_extender_4
  next_field next_field_1 (
    .next_figure(next_figure), .line_1(next_1), .line_2(next_2), .line_3(next_3), .line_4(next_4),
    .line_5(next_5), .line_6(next_6));
  assign xor_1_out = row_20 ^ l20_b;  // XOR_Gate xor_1, 10 bits wide
  Comparator #(.width(10)) comparator_2 (.a(xor_1_out), .b({10{1'b0}}), .eq(comparator_2_eq));  // open: gt, lt
  not not_1 (no_placement, comparator_1_eq);
  Adder #(.width(4)) adder_1 (.a(x), .b(4'b0001), .out(adder_1_out));  // open: cin, cout
  D_Flip_Flop d_ff_1 (.clk(and_1_out), .D(1'b1), .Q(d_ff_1_q), .reset(buffer_1_out));  // open: Qn, preset, en
  buf buffer_1 (buffer_1_out, not_29_out);
  Shifter #(.width(16)) shifter_1 (.in(bit_extender_1_out), .\dist (x), .out(shifter_1_out));
  Shifter #(.width(16)) shifter_2 (.in(bit_extender_2_out), .\dist (x), .out(shifter_2_out));
  Shifter #(.width(16)) shifter_3 (.in(bit_extender_3_out), .\dist (x), .out(shifter_3_out));
  Shifter #(.width(16)) shifter_4 (.in(bit_extender_4_out), .\dist (x), .out(shifter_4_out));
  or or_5 (or_5_out, restart, get_next);
  not not_2 (bottom, comparator_2_eq);
  Register #(.width(4)) register_1 (.D(adder_1_out), .Q(l_x), .clk(or_6_out));  // open: en, clr
  or or_6 (or_6_out, spawn, side_move);
  Register #(.width(4)) register_2 (.D(subtractor_1_out), .Q(r_x), .clk(or_7_out));  // open: en, clr
  Subtractor #(.width(4)) subtractor_1 (.a(x), .b(4'b0001), .out(subtractor_1_out));  // open: bin, bout
  or or_7 (or_7_out, spawn, side_move);
  D_Flip_Flop d_ff_2 (.clk(d_ff_1_q), .D(1'b1), .Q(save), .reset(not_5_out));  // open: Qn, preset, en
  not not_3 (not_3_out, save);
  not not_4 (not_4_out, save);
  not not_5 (not_5_out, not_8_out);
  not not_6 (not_6_out, not_4_out);
  not not_7 (not_7_out, not_3_out);
  not not_8 (not_8_out, not_12_out);
  not not_9 (not_9_out, not_7_out);
  not not_10 (not_10_out, not_6_out);
  not not_11 (not_11_out, not_9_out);
  not not_12 (not_12_out, not_10_out);
  Shifter #(.width(16), .shift("lr")) shifter_5 (.in(shifter_1_out), .\dist (4'b0100), .out(shifter_5_out));
  Bit_Extender #(.in_width(16), .out_width(10)) bit_extender_5 (.in(shifter_5_out), .out(f1));
  Shifter #(.width(16), .shift("lr")) shifter_6 (.in(shifter_2_out), .\dist (4'b0100), .out(shifter_6_out));
  Bit_Extender #(.in_width(16), .out_width(10)) bit_extender_6 (.in(shifter_6_out), .out(f2));
  Shifter #(.width(16), .shift("lr")) shifter_7 (.in(shifter_3_out), .\dist (4'b0100), .out(shifter_7_out));
  Bit_Extender #(.in_width(16), .out_width(10)) bit_extender_7 (.in(shifter_7_out), .out(f3));
  Bit_Extender #(.in_width(16), .out_width(10)) bit_extender_8 (.in(shifter_8_out), .out(f4));
  Shifter #(.width(16), .shift("lr")) shifter_8 (.in(shifter_4_out), .\dist (4'b0100), .out(shifter_8_out));
  D_Flip_Flop d_ff_3 (.clk(or_5_out), .D(1'b1), .Q(d_ff_3_q), .reset(or_8_out));  // open: Qn, preset, en
  or or_8 (or_8_out, game_clk, buffer_4_out);
  Multiplexer #(.width(4)) multiplexer_1 (
    .in0(l_x), .in1(r_x), .out(multiplexer_1_out), .sel(move_right), .en(side_move));
  and and_2 (and_2_out, ~side_move, spawn);  // AND_Gate
  and and_3 (and_3_out, ~collision_left, move_left);  // AND_Gate
  D_Flip_Flop #(.trigger("falling")) d_ff_4 (
    .clk(or_9_out), .D(1'b1), .Q(spawn), .reset(not_13_out));  // open: Qn, preset, en
  or or_9 (or_9_out, not_11_out, restart);
  not not_13 (not_13_out, not_14_out);
  not not_14 (not_14_out, not_25_out);
  assign or_10_out = f4 | f3 | f2 | f1;  // OR_Gate or_10, 10 bits wide
  buf buffer_2 (left_bord, or_10_out[9]);
  buf buffer_3 (right_bord, or_10_out[0]);
  assign bit_extender_9_out = {{7{1'b0}}, d_ff_3_q};  // Bit_Extender bit_extender_9
  buf buffer_4 (buffer_4_out, proc_1_new);
  Multiplexer #(.width(4), .enable("false")) multiplexer_2 (
    .in0(multiplexer_1_out), .in1(4'b0111), .out(multiplexer_2_out), .sel(and_2_out));
  not not_15 (not_15_out, or_12_out);
  or or_11 (or_11_out, spawn, side_move);
  or or_12 (or_12_out, game_over, pause_out);
  or or_13 (side_move, and_3_out, and_4_out);
  and and_4 (and_4_out, move_right, ~collision_right);  // AND_Gate
  not not_16 (not_16_out, not_17_out);
  not not_17 (not_17_out, not_18_out);
  not not_18 (not_18_out, not_20_out);
  not not_19 (not_19_out, not_21_out);
  not not_20 (not_20_out, spawn);
  not not_21 (not_21_out, not_29_out);
  not not_22 (not_22_out, spawn);
  not not_23 (not_23_out, not_22_out);
  not not_24 (not_24_out, not_23_out);
  not not_25 (not_25_out, not_24_out);
  // Probe on f1
  // Probe on f2
  // Probe on f3
  // Probe on f4
  Pull_Resistor pull_resistor_9 (.node(right_bord));
  Pull_Resistor pull_resistor_10 (.node(left_bord));
  proc proc_1 (
    .pause(pause_out), .restart(restart), .game_over(game_over), .\output (proc_1_output), .clk(clk),
    .\input (bit_extender_9_out), .\new (proc_1_new));
  Register #(.width(4), .trigger("falling")) register_3 (
    .D(multiplexer_2_out), .en(not_15_out), .Q(x), .clk(or_11_out));  // open: clr
  Counter counter_1 (.clk(get_next));  // open: load, D, count, Q, carry, clr
  D_Flip_Flop #(.trigger("falling")) d_ff_5 (
    .clk(not_16_out), .D(1'b1), .Q(get_next), .reset(not_19_out));  // open: Qn, preset, en
  not not_26 (not_26_out, get_next);
  not not_27 (not_27_out, not_26_out);
  not not_28 (not_28_out, not_27_out);
  not not_29 (not_29_out, not_28_out);
  // Probe on proc_1_output
  Register register_4 (.D(proc_1_output), .Q(register_4_q), .clk(proc_1_new));  // open: en, clr
  or or_14 (or_14_out, move_right, move_left, rotate);
  Bit_Extender #(.out_width(3)) bit_extender_10 (.in(register_4_q), .out(num));
  Comparator comparator_3 (.a({8{1'b0}}), .b(register_4_q), .eq(comparator_3_eq));  // open: gt, lt
  Register register_5 (.D(register_4_q), .Q(register_5_q), .clk(proc_1_new));  // open: en, clr
  D_Flip_Flop d_ff_6 (.clk(proc_1_new), .D(1'b1), .Q(\new ), .reset(and_5_out));  // open: Qn, preset, en
  and and_5 (and_5_out, or_5_out, \new );
  Counter #(.max('h1f), .trigger("falling")) counter_2 (
    .Q(y), .clk(and_6_out), .clr(spawn));  // open: load, D, count, carry
  and and_6 (and_6_out, game_clk, ~or_14_out, ~or_15_out);  // AND_Gate
  or or_15 (or_15_out, deletion, collision_down);
  // Probe on full_counter
  Comparator #(.mode("unsigned")) comparator_4 (.a(full_counter), .b({8{1'b0}}), .eq(comparator_4_eq));  // open: gt, lt
  assign bit_extender_11_out = {{12{1'b0}}, curr_rotated[3:0]};  // Bit_Extender bit_extender_11
  Shifter #(.width(16)) shifter_9 (.in(bit_extender_11_out), .\dist (x), .out(shifter_9_out));
  assign bit_extender_12_out = {{12{1'b0}}, curr_rotated[7:4]};  // Bit_Extender bit_extender_12
  Shifter #(.width(16)) shifter_10 (.in(bit_extender_12_out), .\dist (x), .out(shifter_10_out));
  assign bit_extender_13_out = {{12{1'b0}}, curr_rotated[11:8]};  // Bit_Extender bit_extender_13
  Shifter #(.width(16)) shifter_11 (.in(bit_extender_13_out), .\dist (x), .out(shifter_11_out));
  assign bit_extender_14_out = {{12{1'b0}}, curr_rotated[15:12]};  // Bit_Extender bit_extender_14
  Shifter #(.width(16)) shifter_12 (.in(bit_extender_14_out), .\dist (x), .out(shifter_12_out));
  or or_16 (or_16_out, comparator_3_eq, comparator_5_eq);
  Comparator comparator_5 (.a(register_4_q), .b(register_5_q), .eq(comparator_5_eq));  // open: gt, lt
  Subtractor subtractor_2 (.a(full_counter), .b(8'h1), .out(subtractor_2_out));  // open: bin, bout
  not not_30 (deletion, comparator_4_eq);
  buf buffer_5 (buffer_5_out, deletion);
  buf buffer_6 (buffer_6_out, comparator_4_eq);
  Multiplexer #(.select(2), .width(16)) multiplexer_3 (
    .in0(16'h1), .in1(16'h3), .in2(16'h7), .in3(16'hf), .out(multiplexer_3_out), .sel(counter), .en(deletion));
  Shifter #(.width(16), .shift("lr")) shifter_13 (.in(shifter_9_out), .\dist (4'b0100), .out(shifter_13_out));
  Shifter #(.width(16), .shift("lr")) shifter_14 (.in(shifter_10_out), .\dist (4'b0100), .out(shifter_14_out));
  Shifter #(.width(16), .shift("lr")) shifter_15 (.in(shifter_11_out), .\dist (4'b0100), .out(shifter_15_out));
  Shifter #(.width(16), .shift("lr")) shifter_16 (.in(shifter_12_out), .\dist (4'b0100), .out(shifter_16_out));
  and and_7 (and_7_out, ~d_ff_3_q, or_16_out);  // AND_Gate
  and and_8 (and_8_out, and_7_out, or_5_out);
  Counter #(.width(9), .max('h1ff)) counter_3 (.carry(game_clk), .clk(clk));  // open: load, D, count, Q, clr
  // Probe on counter
  Bit_Extender #(.out_width(2)) bit_extender_15 (.in(subtractor_2_out), .out(counter));
  D_Flip_Flop d_ff_7 (.clk(deletion), .D(1'b1), .Q(score_en), .reset(and_9_out));  // open: Qn, preset, en
  not not_31 (not_31_out, score_en);
  not not_32 (not_32_out, not_31_out);
  and and_9 (and_9_out, buffer_5_out, game_clk);
  not not_33 (not_33_out, not_32_out);
  not not_34 (not_34_out, not_33_out);
  Register #(.width(16), .trigger("falling")) register_6 (
    .D(multiplexer_4_out), .Q({score3, score2, score1, score0}), .clk(score_en), .clr(restart));  // open: en
  Multiplexer #(.width(16), .enable("false")) multiplexer_4 (
    .in0({score3, score2, score1, score0}), .in1(score_temp), .out(multiplexer_4_out), .sel(deletion));
  bcd_16_bit bcd_16_bit_1 (.A({score3, score2, score1, score0}), .B(multiplexer_3_out), .\С (score_temp));
  Pull_Resistor pull_resistor_11 (.node(multiplexer_3_out));
  assign or_17_out = shifter_13_out | shifter_14_out | shifter_15_out | shifter_16_out;  // OR_Gate or_17, 16 bits wide
  D_Flip_Flop d_ff_8 (.clk(and_8_out), .D(1'b1), .Q(get), .en(not_35_out), .reset(game_clk));  // open: Qn, preset
  not not_35 (not_35_out, \new );
  T_Flip_Flop t_ff_1 (.clk(pause), .T(pause), .Q(pause_out), .en(not_36_out));  // open: Qn, preset, reset
  not not_36 (not_36_out, game_over);
  D_Flip_Flop d_ff_9 (.clk(no_placement), .D(1'b1), .Q(game_over), .reset(restart));  // open: Qn, preset, en
  D_Flip_Flop #(.trigger("falling")) d_ff_10 (
    .clk(not_34_out), .D(1'b1), .Q(d_ff_10_q), .reset(buffer_6_out));  // open: Qn, preset, en
  // Probe on score_temp
  // Probe on fr1
  Bit_Extender #(.in_width(16), .out_width(10)) bit_extender_16 (.in(shifter_13_out), .out(fr1));
  // Probe on fr2
  Bit_Extender #(.in_width(16), .out_width(10)) bit_extender_17 (.in(shifter_14_out), .out(fr2));
  // Probe on fr3
  Bit_Extender #(.in_width(16), .out_width(10)) bit_extender_18 (.in(shifter_15_out), .out(fr3));
  // Probe on fr4
  Bit_Extender #(.in_width(16), .out_width(10)) bit_extender_19 (.in(shifter_16_out), .out(fr4));
  Pull_Resistor pull_resistor_12 (.node(left_bord_r));
  Shifter #(.width(16), .shift("lr")) shifter_17 (.in(or_17_out), .\dist (4'b0001), .out(shifter_17_out));
  buf buffer_7 (left_bord_r, shifter_17_out[9]);
  buf buffer_8 (right_bord_r, shifter_18_out[1]);
  Shifter #(.width(16)) shifter_18 (.in(or_17_out), .\dist (4'b0001), .out(shifter_18_out));
  or or_18 (or_18_out, pause_out, deletion, collision_rotate, game_over);
  and and_10 (delete, d_ff_10_q, clk);
  Pull_Resistor pull_resistor_13 (.node(right_bord_r));
  and and_11 (and_11_out, rotate, ~or_18_out);  // AND_Gate
  Hex_Digit_Display hex_digit_display_1 (.value(score3));  // open: dp
  get_figure get_figure_1 (
    .get_next(get), .curr_figure(curr_figure), .next_figure(next_figure), .rotate(and_11_out),
    .curr_rotate(curr_rotated), .num_gened(num), .save_gened(\new ));
  // Probe on curr_figure
  // Probe on next_figure
  // Probe on curr_rotated
  DotMatrix #(.inputtype("row"), .matrixcols(10), .matrixrows(23)) dotmatrix_1 (
    .row0(l_3), .row1(l_2), .row2(l_1), .row3(row_1), .row4(row_2), .row5(row_3), .row6(row_4), .row7(row_5),
    .row8(row_6), .row9(row_7), .row10(row_8), .row11(row_9), .row12(row_10), .row13(row_11), .row14(row_12),
    .row15(row_13), .row16(row_14), .row17(row_15), .row18(row_16), .row19(row_17), .row20(row_18),
    .row21(row_19), .row22(row_20));
  Hex_Digit_Display hex_digit_display_2 (.value(score1));  // open: dp
  Hex_Digit_Display hex_digit_display_3 (.value(score2));  // open: dp
  Hex_Digit_Display hex_digit_display_4 (.value(score0));  // open: dp

  assign score_1 = 4'b0000;
  assign score_2 = 4'b0000;

  // Other names for the same wires on the sheet: sprite_top[3:0] = curr_figure[3:0];
  //   sprite_topmid[3:0] = curr_figure[7:4]; sprite_botmid[3:0] = curr_figure[11:8];
  //   sprite_bot[3:0] = curr_figure[15:12]; sprite_top_r[3:0] = curr_rotated[3:0];
  //   sprite_topmid_r[3:0] = curr_rotated[7:4]; sprite_botmid_r[3:0] = curr_rotated[11:8];
  //   sprite_bot_r[3:0] = curr_rotated[15:12]; l1[9:0] = row_1; l2[9:0] = row_2; l3[9:0] = row_3; l4[9:0] = row_4;
  //   l5[9:0] = row_5; l6[9:0] = row_6; l7[9:0] = row_7; l8[9:0] = row_8; l9[9:0] = row_9; l10[9:0] = row_10;
  //   l11[9:0] = row_11; l12[9:0] = row_12; l13[9:0] = row_13; l14[9:0] = row_14; l15[9:0] = row_15;
  //   l16[9:0] = row_16; l17[9:0] = row_17; l18[9:0] = row_18; l19[9:0] = row_19; l20[9:0] = row_20; left = move_left;
  //   next1[7:0] = next_1; next2[7:0] = next_2; next3[7:0] = next_3; next4[7:0] = next_4; next5[7:0] = next_5;
  //   next6[7:0] = next_6; pause_state = pause_out; right = move_right; s0[3:0] = score0;
  //   score[15:0] = {score3, score2, score1, score0}; s1[3:0] = score1; s2[3:0] = score2; s3[3:0] = score3

  // Notes on the sheet:
  //   OUTPUTS
  //   MAIN CONTROLLER
  //   CONST-TO-SPRITE CONSTRUCTOR
  //   SIDE MOVER
  //   SPAWN CONTROLLER
  //   buffer_2 drives only 1 and floats otherwise
  //   buffer_3 drives only 1 and floats otherwise
  //   DOWN MOVER
  //   1 row score
  //   2 row score
  //   3 row score
  //   4 row score
  //   DELETION CONTROLLER
  //   CLOCK CONTROLLER
  //   SCORE COUNTER
  //   buffer_7 drives only 1 and floats otherwise
  //   buffer_8 drives only 1 and floats otherwise
  //   INPUTS
endmodule

// sprite ctor
module get_figure (
  input  get_next,
  input  rotate,
  input  save_gened,
  input  [2:0] num_gened,
  output [15:0] curr_figure,
  output [15:0] next_figure,
  output [15:0] curr_rotate
);

  wire comparator_1_eq, not_1_out, not_2_out, not_3_out, not_4_out, or_1_out, or_2_out, or_3_out;
  wire [1:0] curr_rotation;
  wire [2:0] gened_num, multiplexer_6_out, multiplexer_11_out, prev_gened, register_3_q;
  wire [15:0] I_n_pos, I_pos, J_n_pos, J_pos, L_n_pos, L_pos, multiplexer_5_out, multiplexer_12_out, O_n_pos,
       O_pos, rotated_curr, S_n_pos, S_pos, T_n_pos, T_pos, Z_n_pos, Z_pos;

  DotMatrix #(.inputtype("row"), .matrixcols(4), .matrixrows(4)) dotmatrix_1 (
    .row0(curr_figure[3:0]), .row1(curr_figure[7:4]), .row2(curr_figure[11:8]), .row3(curr_figure[15:12]));
  Multiplexer #(.select(2), .width(16), .enable("false")) multiplexer_1 (
    .in0(16'hf0), .in1(16'h2222), .in2(16'hf00), .in3(16'h4444), .out(I_pos), .sel(curr_rotation));
  Multiplexer #(.select(2), .width(16), .enable("false")) multiplexer_2 (
    .in0(16'h6c), .in1(16'h462), .in2(16'h6c0), .in3(16'h8c4), .out(Z_pos), .sel(curr_rotation));
  Multiplexer #(.select(2), .width(16), .enable("false")) multiplexer_3 (
    .in0(16'h2222), .in1(16'hf00), .in2(16'h4444), .in3(16'hf0), .out(I_n_pos), .sel(curr_rotation));
  Multiplexer #(.select(2), .width(16), .enable("false")) multiplexer_4 (
    .in0(16'h462), .in1(16'h6c0), .in2(16'h8c4), .in3(16'h6c), .out(Z_n_pos), .sel(curr_rotation));
  DotMatrix #(.inputtype("row"), .matrixcols(4), .matrixrows(4)) dotmatrix_2 (
    .row0(curr_rotate[3:0]), .row1(curr_rotate[7:4]), .row2(curr_rotate[11:8]), .row3(curr_rotate[15:12]));
  Multiplexer #(.select(3), .width(16), .enable("false")) multiplexer_5 (
    .in0(16'hf0), .in1(16'hf0), .in2(16'he4), .in3(16'h66), .in4(16'hc6), .in5(16'h6c), .in6(16'he8),
    .in7(16'he2), .out(multiplexer_5_out), .sel(multiplexer_6_out));
  not not_1 (not_1_out, or_1_out);
  or or_1 (or_1_out, get_next, save_gened);
  Multiplexer #(.width(3), .enable("false")) multiplexer_6 (
    .in0(gened_num), .in1(num_gened), .out(multiplexer_6_out), .sel(save_gened));
  Multiplexer #(.select(2), .width(16), .enable("false")) multiplexer_7 (
    .in0(16'he4), .in1(16'h464), .in2(16'h4e0), .in3(16'h4c4), .out(T_pos), .sel(curr_rotation));
  Multiplexer #(.select(2), .width(16), .enable("false")) multiplexer_8 (
    .in0(16'he8), .in1(16'h446), .in2(16'h2e0), .in3(16'hc44), .out(J_pos), .sel(curr_rotation));
  Multiplexer #(.select(2), .width(16), .enable("false")) multiplexer_9 (
    .in0(16'h464), .in1(16'h4e0), .in2(16'h4c4), .in3(16'he4), .out(T_n_pos), .sel(curr_rotation));
  Multiplexer #(.select(2), .width(16), .enable("false")) multiplexer_10 (
    .in0(16'h446), .in1(16'h2e0), .in2(16'hc44), .in3(16'he8), .out(J_n_pos), .sel(curr_rotation));
  Register #(.width(16)) register_1 (.D(multiplexer_5_out), .Q(next_figure), .clk(not_1_out));  // open: en, clr
  Multiplexer #(.width(3), .enable("false")) multiplexer_11 (
    .in0(gened_num), .in1(num_gened), .out(multiplexer_11_out), .sel(save_gened));
  Random #(.width(3), .trigger("falling")) random_1 (.clk(get_next), .out(gened_num));  // open: next, clr
  Counter #(.width(2), .max('h3)) counter_1 (
    .Q(curr_rotation), .clk(rotate), .clr(get_next));  // open: load, D, count, carry
  Multiplexer #(.width(16), .enable("false")) multiplexer_12 (
    .in0(next_figure), .in1(rotated_curr), .out(multiplexer_12_out), .sel(rotate));
  Register #(.width(16)) register_2 (.D(multiplexer_12_out), .Q(curr_figure), .clk(not_2_out));  // open: en, clr
  not not_2 (not_2_out, or_2_out);
  or or_2 (or_2_out, get_next, save_gened, rotate);
  Register #(.width(3), .trigger("falling")) register_3 (
    .D(multiplexer_11_out), .Q(register_3_q), .clk(or_3_out));  // open: en, clr
  Register #(.width(3), .trigger("falling")) register_4 (
    .D(register_3_q), .Q(prev_gened), .clk(not_3_out));  // open: en, clr
  not not_3 (not_3_out, or_3_out);
  or or_3 (or_3_out, get_next, save_gened);
  Multiplexer #(.select(2), .width(16), .enable("false")) multiplexer_13 (
    .in0(16'h66), .in1(16'h66), .in2(16'h66), .in3(16'h66), .out(O_pos), .sel(curr_rotation));
  Multiplexer #(.select(2), .width(16), .enable("false")) multiplexer_14 (
    .in0(16'he2), .in1(16'h644), .in2(16'h8e0), .in3(16'h44c), .out(L_pos), .sel(curr_rotation));
  Multiplexer #(.select(2), .width(16), .enable("false")) multiplexer_15 (
    .in0(16'h66), .in1(16'h66), .in2(16'h66), .in3(16'h66), .out(O_n_pos), .sel(curr_rotation));
  Multiplexer #(.select(2), .width(16), .enable("false")) multiplexer_16 (
    .in0(16'h644), .in1(16'h8e0), .in2(16'h44c), .in3(16'he2), .out(L_n_pos), .sel(curr_rotation));
  Multiplexer #(.select(2), .width(16), .enable("false")) multiplexer_17 (
    .in0(16'hc6), .in1(16'h264), .in2(16'hc60), .in3(16'h4c8), .out(S_pos), .sel(curr_rotation));
  Multiplexer #(.select(2), .width(16), .enable("false")) multiplexer_18 (
    .in0(16'h264), .in1(16'hc60), .in2(16'h4c8), .in3(16'hc6), .out(S_n_pos), .sel(curr_rotation));
  Multiplexer #(.select(3), .width(16), .enable("false")) multiplexer_19 (
    .in0(I_pos), .in1(I_pos), .in2(T_pos), .in3(O_pos), .in4(S_pos), .in5(Z_pos), .in6(J_pos), .in7(L_pos),
    .out(rotated_curr), .sel(prev_gened));
  Pull_Resistor pull_resistor_1 (.node(curr_rotate));
  Multiplexer #(.select(3), .width(16)) multiplexer_20 (
    .in0(I_n_pos), .in1(I_n_pos), .in2(T_n_pos), .in3(O_n_pos), .in4(S_n_pos), .in5(Z_n_pos), .in6(J_n_pos),
    .in7(L_n_pos), .out(curr_rotate), .sel(prev_gened), .en(not_4_out));
  Comparator #(.width(16)) comparator_1 (.a(curr_figure), .b({16{1'b0}}), .eq(comparator_1_eq));  // open: gt, lt
  not not_4 (not_4_out, comparator_1_eq);

  // Other names for the same wires on the sheet: next_rotation[15:0] = curr_rotate; num[2:0] = num_gened;
  //   save = save_gened

  // Notes on the sheet:
  //   0
  //   INPUTS
  //   OUTPUTS
  //   FIGURE SET
  //   90
  //   ROTATION SETS
  //   180
  //   270
  //   FIGURE ROTATION CONTROLLER
  //    GET NEXT ROTATION
  //   SPRITE CONTROLLER
endmodule

// mover
module sprite_mover (
  input  [7:0] line_in,
  input  [7:0] y_placement,
  input  [9:0] sprite_top,
  input  [9:0] sprite_topmid,
  input  [9:0] sprite_botmid,
  input  [9:0] sprite_bottom,
  input  [9:0] full_row_in,
  input  [7:0] full_count_in,
  input  save_to_background,
  input  delete_row,
  input  erase,
  input  [9:0] sprite_top_2,
  input  [9:0] sprite_topmid_2,
  input  [9:0] sprite_botmid_2,
  input  [9:0] sprite_bottom_2,
  output [7:0] next_line,
  output [9:0] background_out,
  output [9:0] out,
  output [9:0] row_out,
  output [7:0] full_count_out
);

  wire and_1_out, and_2_out, and_3_out, comparator_1_eq, comparator_2_eq, comparator_3_lt, comparator_4_lt,
       comparator_5_lt, comparator_6_lt, or_2_out;
  wire [1:0] bit_extender_1_out, bit_extender_2_out;
  wire [7:0] subtractor_1_out, subtractor_2_out;
  wire [9:0] check, multiplexer_2_out, rotated;

  Adder adder_1 (.a(line_in), .b(8'h1), .out(next_line));  // open: cin, cout
  Comparator #(.width(10)) comparator_1 (.a(background_out), .b({10{1'b1}}), .eq(comparator_1_eq));  // open: gt, lt
  Adder adder_2 (.a(full_count_in), .b({8{1'b0}}), .out(full_count_out), .cin(comparator_1_eq));  // open: cout
  Subtractor subtractor_1 (.a(line_in), .b(y_placement), .out(subtractor_1_out));  // open: bin, bout
  Bit_Extender #(.out_width(2)) bit_extender_1 (.in(subtractor_1_out), .out(bit_extender_1_out));
  assign row_out = check | background_out;  // OR_Gate or_1, 10 bits wide
  Comparator comparator_2 (.a(full_count_in), .b({8{1'b0}}), .eq(comparator_2_eq));  // open: gt, lt
  Comparator comparator_3 (.a({8{1'b1}}), .b(subtractor_1_out), .lt(comparator_3_lt));  // open: gt, eq
  Comparator comparator_4 (.a(subtractor_1_out), .b(8'h4), .lt(comparator_4_lt));  // open: gt, eq
  Multiplexer #(.select(2), .width(10), .disabled(0)) multiplexer_1 (
    .in0(sprite_top), .in1(sprite_topmid), .in2(sprite_botmid), .in3(sprite_bottom), .out(check),
    .sel(bit_extender_1_out), .en(and_2_out));
  Multiplexer #(.width(10), .enable("false")) multiplexer_2 (
    .in0(row_out), .in1(full_row_in), .out(multiplexer_2_out), .sel(and_1_out));
  or or_2 (or_2_out, and_1_out, save_to_background);
  and and_1 (and_1_out, comparator_2_eq, delete_row);
  and and_2 (and_2_out, comparator_3_lt, comparator_4_lt);
  Register #(.width(10), .trigger("falling")) register_1 (
    .D(multiplexer_2_out), .Q(background_out), .clk(or_2_out), .clr(erase));  // open: en
  Subtractor subtractor_2 (.a(line_in), .b(y_placement), .out(subtractor_2_out));  // open: bin, bout
  Comparator comparator_5 (.a({8{1'b1}}), .b(subtractor_2_out), .lt(comparator_5_lt));  // open: gt, eq
  Comparator comparator_6 (.a(subtractor_2_out), .b(8'h4), .lt(comparator_6_lt));  // open: gt, eq
  Bit_Extender #(.out_width(2)) bit_extender_2 (.in(subtractor_2_out), .out(bit_extender_2_out));
  Multiplexer #(.select(2), .width(10), .disabled(0)) multiplexer_3 (
    .in0(sprite_top_2), .in1(sprite_topmid_2), .in2(sprite_botmid_2), .in3(sprite_bottom_2), .out(rotated),
    .sel(bit_extender_2_out), .en(and_3_out));
  and and_3 (and_3_out, comparator_5_lt, comparator_6_lt);

  assign out = background_out;

  // Other names for the same wires on the sheet: count_in[7:0] = full_count_in; count_out[7:0] = full_count_out;
  //   delete = delete_row; f1[9:0] = sprite_top; f2[9:0] = sprite_topmid; f3[9:0] = sprite_botmid;
  //   f4[9:0] = sprite_bottom; fr1[9:0] = sprite_top_2; fr2[9:0] = sprite_topmid_2; fr3[9:0] = sprite_botmid_2;
  //   fr4[9:0] = sprite_bottom_2; row_in[9:0] = full_row_in; save = save_to_background; y[7:0] = y_placement

  // Notes on the sheet:
  //   y_placement: pull=down
  //   full_count_in: pull=down
  //   full_row_in: pull=down
  //   delete_row: pull=down
  //   line_in: pull=down
  //   INPUTS
  //   OUTPUTS
  //   NEXT LINE
  //   FULL LINES COUNTER
  //   FIGURE LINE PLACEMENT
  //   SAVE AND DELETE
endmodule

module collision (
  input  [7:0] line_in,
  input  [7:0] y_placement,
  input  [9:0] sprite_top,
  input  [9:0] r_sprite_top,
  input  [9:0] sprite_topmid,
  input  [9:0] r_sprite_topmid,
  input  [9:0] sprite_botmid,
  input  [9:0] r_sprite_botmid,
  input  [9:0] sprite_bottom,
  input  [9:0] r_sprite_bot,
  input  [9:0] background_row,
  output [7:0] next_line,
  output collision_rotate,
  output collision_left,
  output collision_right,
  output collision_down
);

  wire and_2_out, and_3_out, and_4_out, and_8_out, comparator_1_lt, comparator_2_lt, comparator_3_eq,
       comparator_4_lt, comparator_5_lt, comparator_6_lt, comparator_7_lt, comparator_8_lt, comparator_9_lt,
       comparator_10_eq, comparator_11_eq, comparator_12_eq, comparator_13_eq, comparator_14_eq, down_r,
       left_r, right_r;
  wire [1:0] bit_extender_1_out, bit_extender_2_out, bit_extender_3_out, bit_extender_4_out;
  wire [7:0] check_line, down_line, down_line_r, subtractor_1_out, subtractor_2_out, subtractor_3_out,
       subtractor_4_out;
  wire [9:0] and_1_out, and_5_out, and_6_out, and_7_out, and_9_out, and_10_out, bot_check, bot_check_r,
       shifter_1_out, shifter_2_out, shifter_3_out, shifter_4_out, side_check, side_r_check;

  Subtractor subtractor_1 (.a(down_line), .b(y_placement), .out(subtractor_1_out));  // open: bin, bout
  Subtractor subtractor_2 (.a(check_line), .b(y_placement), .out(subtractor_2_out));  // open: bin, bout
  Subtractor subtractor_3 (.a(down_line_r), .b(y_placement), .out(subtractor_3_out));  // open: bin, bout
  Adder adder_1 (.a(line_in), .b(8'h1), .out(next_line));  // open: cin, cout
  Adder adder_2 (.a(next_line), .b(8'h2), .out(down_line));  // open: cin, cout
  Adder adder_3 (.a(line_in), .b(8'h4), .out(check_line));  // open: cin, cout
  Adder adder_4 (.a(next_line), .b(8'h3), .out(down_line_r));  // open: cin, cout
  Comparator comparator_1 (.a({8{1'b1}}), .b(subtractor_1_out), .lt(comparator_1_lt));  // open: gt, eq
  Comparator comparator_2 (.a(subtractor_1_out), .b(8'h4), .lt(comparator_2_lt));  // open: gt, eq
  Bit_Extender #(.out_width(2)) bit_extender_1 (.in(subtractor_1_out), .out(bit_extender_1_out));
  assign and_1_out = bot_check & background_row;  // AND_Gate and_1, 10 bits wide
  Comparator #(.width(10)) comparator_3 (.a(and_1_out), .b({10{1'b0}}), .eq(comparator_3_eq));  // open: gt, lt
  Comparator comparator_4 (.a({8{1'b1}}), .b(subtractor_2_out), .lt(comparator_4_lt));  // open: gt, eq
  Comparator comparator_5 (.a(subtractor_2_out), .b(8'h4), .lt(comparator_5_lt));  // open: gt, eq
  Bit_Extender #(.out_width(2)) bit_extender_2 (.in(subtractor_2_out), .out(bit_extender_2_out));
  Comparator comparator_6 (.a({8{1'b1}}), .b(subtractor_3_out), .lt(comparator_6_lt));  // open: gt, eq
  Comparator comparator_7 (.a(subtractor_3_out), .b(8'h4), .lt(comparator_7_lt));  // open: gt, eq
  Bit_Extender #(.out_width(2)) bit_extender_3 (.in(subtractor_3_out), .out(bit_extender_3_out));
  and and_2 (and_2_out, comparator_1_lt, comparator_2_lt);
  Multiplexer #(.select(2), .width(10), .disabled(0)) multiplexer_1 (
    .in0(sprite_top), .in1(sprite_topmid), .in2(sprite_botmid), .in3(sprite_bottom), .out(bot_check),
    .sel(bit_extender_1_out), .en(and_2_out));
  not not_1 (collision_down, comparator_3_eq);
  and and_3 (and_3_out, comparator_4_lt, comparator_5_lt);
  Multiplexer #(.select(2), .width(10), .disabled(0)) multiplexer_2 (
    .in0(r_sprite_top), .in1(r_sprite_topmid), .in2(r_sprite_botmid), .in3(r_sprite_bot), .out(side_r_check),
    .sel(bit_extender_2_out), .en(and_3_out));
  and and_4 (and_4_out, comparator_6_lt, comparator_7_lt);
  Multiplexer #(.select(2), .width(10), .disabled(0)) multiplexer_3 (
    .in0(r_sprite_top), .in1(r_sprite_topmid), .in2(r_sprite_botmid), .in3(r_sprite_bot), .out(bot_check_r),
    .sel(bit_extender_3_out), .en(and_4_out));
  Subtractor subtractor_4 (.a(check_line), .b(y_placement), .out(subtractor_4_out));  // open: bin, bout
  Shifter #(.width(10)) shifter_1 (.in(side_check), .\dist (4'b0001), .out(shifter_1_out));
  Shifter #(.width(10), .shift("lr")) shifter_2 (.in(side_check), .\dist (4'b0001), .out(shifter_2_out));
  Shifter #(.width(10)) shifter_3 (.in(side_r_check), .\dist (4'b0010), .out(shifter_3_out));
  Shifter #(.width(10), .shift("lr")) shifter_4 (.in(side_r_check), .\dist (4'b0010), .out(shifter_4_out));
  Comparator comparator_8 (.a({8{1'b1}}), .b(subtractor_4_out), .lt(comparator_8_lt));  // open: gt, eq
  Comparator comparator_9 (.a(subtractor_4_out), .b(8'h4), .lt(comparator_9_lt));  // open: gt, eq
  Bit_Extender #(.out_width(2)) bit_extender_4 (.in(subtractor_4_out), .out(bit_extender_4_out));
  assign and_5_out = shifter_1_out & background_row;  // AND_Gate and_5, 10 bits wide
  Comparator #(.width(10)) comparator_10 (.a(and_5_out), .b({10{1'b0}}), .eq(comparator_10_eq));  // open: gt, lt
  assign and_6_out = shifter_2_out & background_row;  // AND_Gate and_6, 10 bits wide
  Comparator #(.width(10)) comparator_11 (.a(and_6_out), .b({10{1'b0}}), .eq(comparator_11_eq));  // open: gt, lt
  assign and_7_out = bot_check_r & background_row;  // AND_Gate and_7, 10 bits wide
  or or_1 (collision_rotate, right_r, down_r, left_r);
  and and_8 (and_8_out, comparator_8_lt, comparator_9_lt);
  Multiplexer #(.select(2), .width(10), .disabled(0)) multiplexer_4 (
    .in0(sprite_top), .in1(sprite_topmid), .in2(sprite_botmid), .in3(sprite_bottom), .out(side_check),
    .sel(bit_extender_4_out), .en(and_8_out));
  not not_2 (collision_left, comparator_10_eq);
  not not_3 (collision_right, comparator_11_eq);
  assign and_9_out = shifter_3_out & background_row;  // AND_Gate and_9, 10 bits wide
  Comparator #(.width(10)) comparator_12 (.a(and_9_out), .b({10{1'b0}}), .eq(comparator_12_eq));  // open: gt, lt
  assign and_10_out = shifter_4_out & background_row;  // AND_Gate and_10, 10 bits wide
  Comparator #(.width(10)) comparator_13 (.a(and_10_out), .b({10{1'b0}}), .eq(comparator_13_eq));  // open: gt, lt
  Pull_Resistor pull_resistor_1 (.node(down_r));
  not not_4 (down_r, comparator_14_eq);
  Comparator #(.width(10)) comparator_14 (.a(and_7_out), .b({10{1'b0}}), .eq(comparator_14_eq));  // open: gt, lt
  Pull_Resistor pull_resistor_2 (.node(left_r));
  not not_5 (left_r, comparator_12_eq);
  not not_6 (right_r, comparator_13_eq);
  Pull_Resistor pull_resistor_3 (.node(right_r));

  // Other names for the same wires on the sheet: background[9:0] = background_row; down = collision_down;
  //   f1[9:0] = sprite_top; f2[9:0] = sprite_topmid; f3[9:0] = sprite_botmid; f4[9:0] = sprite_bottom;
  //   fr1[9:0] = r_sprite_top; fr2[9:0] = r_sprite_topmid; fr3[9:0] = r_sprite_botmid; fr4[9:0] = r_sprite_bot;
  //   left = collision_left; right = collision_right; rotate = collision_rotate; y[7:0] = y_placement

  // Notes on the sheet:
  //   y_placement: pull=down
  //   line_in: pull=down
  //   INPUTS
  //   OUTPUTS
  //   NEXT LINES
  //   BOTTOM COLLISION
  //   ROTATION COLLISION
  //   not_1 drives only 1 and floats otherwise
  //   SIDES COLLISION
  //   LEFT COLLISION
  //   RIGHT COLLISION
  //   LEFT ROTATE COLLISION
  //   RIGHT ROTATE COLLISION
  //   BOTTOM ROTATE COLLISION
  //   not_2 drives only 1 and floats otherwise
  //   not_3 drives only 1 and floats otherwise
  //   not_4 drives only 1 and floats otherwise
  //   not_5 drives only 1 and floats otherwise
  //   not_6 drives only 1 and floats otherwise
endmodule

// next-disp
module next_field (
  input  [15:0] next_figure,
  output [7:0] line_1,
  output [7:0] line_2,
  output [7:0] line_3,
  output [7:0] line_4,
  output [7:0] line_5,
  output [7:0] line_6
);


  assign line_1 = {8{1'b0}};
  assign line_2 = {8{1'b0}};
  assign line_3 = {2'b00, next_figure[3:0], 2'b00};
  assign line_4 = {2'b00, next_figure[7:4], 2'b00};
  assign line_5 = {8{1'b0}};
  assign line_6 = {8{1'b0}};

  // Other names for the same wires on the sheet: f1[3:0] = next_figure[3:0]; l3[5:2] = next_figure[3:0];
  //   next[15:0] = next_figure; f2[3:0] = next_figure[7:4]; l4[5:2] = next_figure[7:4]

  // Notes on the sheet:
  //   INPUTS
  //   OUTPUTS
endmodule

// BCD-add
module bcd_adder (
  input  Cin,
  input  [3:0] A,
  input  [3:0] B,
  output [3:0] \С ,
  output Cout
);

  wire and_1_out, and_2_out, full_4_bit_adder_1_cout;
  wire [3:0] full_4_bit_adder_1_c;
  wire [3:3] pull_resistor_1_node;

  full_4_bit_adder full_4_bit_adder_1 (
    .A(A), .B(B), .cin(Cin), .C(full_4_bit_adder_1_c), .cout(full_4_bit_adder_1_cout));
  // Probe on full_4_bit_adder_1_c
  and and_1 (and_1_out, full_4_bit_adder_1_c[2], full_4_bit_adder_1_c[3]);
  and and_2 (and_2_out, full_4_bit_adder_1_c[1], full_4_bit_adder_1_c[3]);
  Pull_Resistor pull_resistor_1 (.node(pull_resistor_1_node[3]));
  or or_1 (Cout, and_1_out, full_4_bit_adder_1_cout, and_2_out);
  // Probe on \С 
  full_4_bit_adder full_4_bit_adder_2 (
    .A(full_4_bit_adder_1_c), .B({pull_resistor_1_node[3], {2{Cout}}, pull_resistor_1_node[3]}),
    .cin(pull_resistor_1_node[3]), .C(\С ));  // open: cout
endmodule

// BCD 16bit
module bcd_16_bit (
  input  [15:0] A,
  input  [15:0] B,
  output [15:0] \С 
);

  wire bcd_adder_1_cout, bcd_adder_2_cout, bcd_adder_3_cout, comparator_1_gt, comparator_2_gt,
       comparator_3_gt, comparator_4_gt;
  wire [3:0] adder_1_out, adder_2_out, adder_3_out, \bcd_adder_1_с , \bcd_adder_2_с , \bcd_adder_3_с ,
       \bcd_adder_4_с , multiplexer_1_out, multiplexer_2_out, multiplexer_3_out, subtractor_1_out,
       subtractor_2_out, subtractor_3_out, subtractor_4_out;

  Hex_Digit_Display hex_digit_display_1 (.value(\С [15:12]));  // open: dp
  Pull_Resistor pull_resistor_1 (.node(A));
  Pull_Resistor pull_resistor_2 (.node(B));
  Hex_Digit_Display hex_digit_display_2 (.value(\С [7:4]));  // open: dp
  Hex_Digit_Display hex_digit_display_3 (.value(\С [11:8]));  // open: dp
  Hex_Digit_Display hex_digit_display_4 (.value(A[11:8]));  // open: dp
  Hex_Digit_Display hex_digit_display_5 (.value(A[15:12]));  // open: dp
  Hex_Digit_Display hex_digit_display_6 (.value(B[11:8]));  // open: dp
  Hex_Digit_Display hex_digit_display_7 (.value(B[15:12]));  // open: dp
  Hex_Digit_Display hex_digit_display_8 (.value(\С [3:0]));  // open: dp
  Hex_Digit_Display hex_digit_display_9 (.value(A[7:4]));  // open: dp
  Hex_Digit_Display hex_digit_display_10 (.value(A[3:0]));  // open: dp
  Hex_Digit_Display hex_digit_display_11 (.value(B[7:4]));  // open: dp
  Hex_Digit_Display hex_digit_display_12 (.value(B[3:0]));  // open: dp
  bcd_adder bcd_adder_1 (.A(A[3:0]), .B(B[3:0]), .Cin(1'b0), .\С (\bcd_adder_1_с ), .Cout(bcd_adder_1_cout));
  bcd_adder bcd_adder_2 (
    .A(A[7:4]), .B(B[7:4]), .Cin(bcd_adder_1_cout), .\С (\bcd_adder_2_с ), .Cout(bcd_adder_2_cout));
  bcd_adder bcd_adder_3 (
    .A(A[11:8]), .B(B[11:8]), .Cin(bcd_adder_2_cout), .\С (\bcd_adder_3_с ), .Cout(bcd_adder_3_cout));
  bcd_adder bcd_adder_4 (.A(A[15:12]), .B(B[15:12]), .Cin(bcd_adder_3_cout), .\С (\bcd_adder_4_с ));  // open: Cout
  // Probe on \bcd_adder_1_с 
  Adder #(.width(4)) adder_1 (.a(\bcd_adder_2_с ), .b(4'b0001), .out(adder_1_out));  // open: cin, cout
  Adder #(.width(4)) adder_2 (.a(\bcd_adder_3_с ), .b(4'b0001), .out(adder_2_out));  // open: cin, cout
  Adder #(.width(4)) adder_3 (.a(\bcd_adder_4_с ), .b(4'b0001), .out(adder_3_out));  // open: cin, cout
  Multiplexer #(.width(4), .enable("false")) multiplexer_1 (
    .in0(\bcd_adder_2_с ), .in1(adder_1_out), .out(multiplexer_1_out), .sel(comparator_1_gt));
  Multiplexer #(.width(4), .enable("false")) multiplexer_2 (
    .in0(\bcd_adder_3_с ), .in1(adder_2_out), .out(multiplexer_2_out), .sel(comparator_2_gt));
  Multiplexer #(.width(4), .enable("false")) multiplexer_3 (
    .in0(\bcd_adder_4_с ), .in1(adder_3_out), .out(multiplexer_3_out), .sel(comparator_3_gt));
  Comparator #(.width(4), .mode("unsigned")) comparator_1 (
    .a(\bcd_adder_1_с ), .b(4'b1001), .gt(comparator_1_gt));  // open: eq, lt
  Comparator #(.width(4), .mode("unsigned")) comparator_2 (
    .a(multiplexer_1_out), .b(4'b1001), .gt(comparator_2_gt));  // open: eq, lt
  Comparator #(.width(4), .mode("unsigned")) comparator_3 (
    .a(multiplexer_2_out), .b(4'b1001), .gt(comparator_3_gt));  // open: eq, lt
  Comparator #(.width(4), .mode("unsigned")) comparator_4 (
    .a(multiplexer_3_out), .b(4'b1001), .gt(comparator_4_gt));  // open: eq, lt
  Subtractor #(.width(4)) subtractor_1 (.a(\bcd_adder_1_с ), .b(4'b1010), .out(subtractor_1_out));  // open: bin, bout
  Subtractor #(.width(4)) subtractor_2 (.a(multiplexer_1_out), .b(4'b1010), .out(subtractor_2_out));  // open: bin, bout
  Subtractor #(.width(4)) subtractor_3 (.a(multiplexer_2_out), .b(4'b1010), .out(subtractor_3_out));  // open: bin, bout
  Subtractor #(.width(4)) subtractor_4 (.a(multiplexer_3_out), .b(4'b1010), .out(subtractor_4_out));  // open: bin, bout
  Multiplexer #(.width(4), .enable("false")) multiplexer_4 (
    .in0(\bcd_adder_1_с ), .in1(subtractor_1_out), .out(\С [3:0]), .sel(comparator_1_gt));
  Multiplexer #(.width(4), .enable("false")) multiplexer_5 (
    .in0(multiplexer_1_out), .in1(subtractor_2_out), .out(\С [7:4]), .sel(comparator_2_gt));
  Multiplexer #(.width(4), .enable("false")) multiplexer_6 (
    .in0(multiplexer_2_out), .in1(subtractor_3_out), .out(\С [11:8]), .sel(comparator_3_gt));
  Multiplexer #(.width(4), .enable("false")) multiplexer_7 (
    .in0(multiplexer_3_out), .in1(subtractor_4_out), .out(\С [15:12]), .sel(comparator_4_gt));

  // Other names for the same wires on the sheet: a0[3:0] = A[3:0]; a1[3:0] = A[7:4]; a2[3:0] = A[11:8];
  //   a3[3:0] = A[15:12]; b0[3:0] = B[3:0]; b1[3:0] = B[7:4]; b2[3:0] = B[11:8]; b3[3:0] = B[15:12];
  //   c2[3:0] = \С [11:8]; c3[3:0] = \С [15:12]; c0[3:0] = \С [3:0]; c1[3:0] = \С [7:4]
endmodule

// add
module full_4_bit_adder (
  input  [3:0] A,
  input  [3:0] B,
  input  cin,
  output [3:0] C,
  output cout
);

  wire adder_1_cout, adder_2_cout, adder_3_cout;

  Adder #(.width(1)) adder_1 (.a(A[0]), .b(B[0]), .out(C[0]), .cin(cin), .cout(adder_1_cout));
  Adder #(.width(1)) adder_2 (.a(A[1]), .b(B[1]), .out(C[1]), .cin(adder_1_cout), .cout(adder_2_cout));
  Adder #(.width(1)) adder_3 (.a(A[2]), .b(B[2]), .out(C[2]), .cin(adder_2_cout), .cout(adder_3_cout));
  Adder #(.width(1)) adder_4 (.a(A[3]), .b(B[3]), .out(C[3]), .cin(adder_3_cout), .cout(cout));
endmodule
